// Logisim project ESF.circ as structural Verilog: 12 circuits, main circuit main
module main (
  input  [2:0] in_1,
  input  in_2,
  input  [3:0] in_3,
  input  in_4,
  input  in_5,
  input  [4:0] in_6,
  input  [4:0] in_7,
  input  in_8,
  output [15:0] out_9,
  output halt,
  output [31:0] out_11,
  output [31:0] out_12
);

  wire and_1_out, and_2_out, and_4_out, clock_1_out, not_2_out, not_3_out, not_10_out, or_2_out;
  wire [0:0] not_1_out, not_9_out;
  wire [1:0] counter_1_q, not_5_out;
  wire [1:1] not_8_out;
  wire [2:2] not_6_out;
  wire [4:0] adder_1_out, and_3_out, counter_2_q, not_11_out, or_1_out;
  wire [15:0] esfkeyt_1_out_6, multiplexer_7_out, ram_3_data, ram_3_data_2, ram_5_data, ram_5_data_2;
  wire [31:0] esfkeyt_1_out_7, esfkeyt_1_out_8, multiplexer_1_out, multiplexer_4_out, multiplexer_5_out,
       multiplexer_6_out, ram_1_data, ram_2_data, register_1_q, register_2_q, roundfunction_1_out_3,
       shift7_1_out_2, xor_1_out;
  wire [31:16] ram_4_data, ram_4_data_2;

  not not_1 (not_1_out[0], in_1[0]);
  Counter #(.width(2), .max('h2), .ongoal("stay")) counter_1 (
    .load(in_1[2]), .Q(counter_1_q), .clk(clock_1_out));  // open: D, count, carry, clr
  Clock clock_1 (.out(clock_1_out));
  and and_1 (and_1_out, counter_1_q[1], clock_1_out);
  not not_2 (not_2_out, not_10_out);
  RAM #(.addrWidth(3), .dataWidth(32)) ram_1 (
    .addr({in_1[2:1], not_1_out[0]}), .data(ram_1_data), .clk(and_1_out), .ld(not_3_out));  // open: sel, clr
  not not_3 (not_3_out, in_2);
  Multiplexer #(.width(32)) multiplexer_1 (
    .in0(ram_1_data), .in1(register_2_q), .out(multiplexer_1_out), .sel(or_2_out));  // open: en
  shift7 shift7_1 (.in_1(multiplexer_1_out), .out_2(shift7_1_out_2));
  Register #(.width(32)) register_1 (.D(xor_1_out), .en(not_10_out), .Q(register_1_q), .clk(and_1_out));  // open: clr
  Multiplexer #(.width(32)) multiplexer_2 (.in0(xor_1_out), .sel(in_8), .en(not_2_out));  // open: in1, out
  assign xor_1_out = shift7_1_out_2 ^ roundfunction_1_out_3;  // XOR_Gate xor_1, 32 bits wide
  Multiplexer #(.width(32)) multiplexer_3 (.in0(multiplexer_4_out), .sel(in_8), .en(not_2_out));  // open: in1, out
  not not_4 (not_5_out[1], in_1[1]);
  not not_5 (not_5_out[0], in_1[0]);
  RAM #(.addrWidth(3), .dataWidth(32)) ram_2 (
    .addr(in_1), .data(ram_2_data), .clk(and_1_out), .ld(not_3_out));  // open: sel, clr
  not not_6 (not_6_out[2], in_1[2]);
  RoundFunction roundfunction_1 (.in_1(multiplexer_4_out), .in_2(multiplexer_5_out), .out_3(roundfunction_1_out_3));
  Register #(.width(32)) register_2 (
    .D(multiplexer_4_out), .en(not_10_out), .Q(register_2_q), .clk(and_1_out));  // open: clr
  Multiplexer #(.width(32)) multiplexer_4 (
    .in0(ram_2_data), .in1(register_1_q), .out(multiplexer_4_out), .sel(or_2_out));  // open: en
  RAM #(.addrWidth(3), .dataWidth(32)) ram_3 (
    .addr({in_1[2], not_5_out}), .data({ram_3_data, ram_3_data_2}), .clk(and_1_out), .ld(not_3_out));  // open: sel, clr
  RAM #(.addrWidth(3), .dataWidth(32)) ram_4 (
    .addr({not_6_out[2], in_1[1:0]}), .data({ram_4_data, ram_4_data_2}), .clk(and_1_out), .ld(not_3_out));  // open: sel, clr
  not not_7 (halt, not_10_out);
  not not_8 (not_8_out[1], in_1[1]);
  not not_9 (not_9_out[0], in_4);
  Counter #(.width(5), .max('h1f), .ongoal("stay")) counter_2 (
    .load(in_5), .count(and_2_out), .Q(counter_2_q), .clk(and_1_out));  // open: D, carry, clr
  assign or_1_out = counter_2_q | in_6;  // OR_Gate or_1, 5 bits wide
  or or_2 (or_2_out, or_1_out[4], or_1_out[3], or_1_out[2], or_1_out[1], or_1_out[0]);
  and and_2 (and_2_out, counter_1_q[1], not_10_out);
  Multiplexer #(.width(32)) multiplexer_5 (
    .in0({ram_4_data_2, ram_3_data}), .in1(out_12), .out(multiplexer_5_out), .sel(or_2_out));  // open: en
  Multiplexer #(.width(32)) multiplexer_6 (
    .in0({ram_3_data_2, ram_5_data_2}), .in1(out_11), .out(multiplexer_6_out), .sel(or_2_out));  // open: en
  esfKeyT esfkeyt_1 (
    .in_2(in_5), .in_5(multiplexer_5_out), .in_3(multiplexer_6_out), .in_1(multiplexer_7_out),
    .out_8(esfkeyt_1_out_8), .out_7(esfkeyt_1_out_7), .out_6(esfkeyt_1_out_6), .counter(adder_1_out));
  not not_10 (not_10_out, and_4_out);
  RAM #(.addrWidth(3), .dataWidth(32)) ram_5 (
    .addr({in_1[2], not_8_out[1], in_1[0]}), .data({ram_5_data_2, ram_5_data}), .clk(and_1_out),
    .ld(not_3_out));  // open: sel, clr
  Multiplexer #(.width(16)) multiplexer_7 (
    .in0(ram_5_data), .in1(out_9), .out(multiplexer_7_out), .sel(or_2_out));  // open: en
  Adder #(.width(5)) adder_1 (.a(counter_2_q), .b({in_3, not_9_out[0]}), .out(adder_1_out));  // open: cin, cout
  assign not_11_out = ~in_7;  // NOT_Gate not_11, 5 bits wide
  assign and_3_out = counter_2_q & not_11_out;  // AND_Gate and_3, 5 bits wide
  and and_4 (and_4_out, and_3_out[4], and_3_out[3], and_3_out[2], and_3_out[1], and_3_out[0]);
  Register #(.width(16)) register_3 (.D(esfkeyt_1_out_6), .en(not_10_out), .Q(out_9), .clk(and_1_out));  // open: clr
  Register #(.width(32)) register_4 (.D(esfkeyt_1_out_7), .en(not_10_out), .Q(out_11), .clk(and_1_out));  // open: clr
  Register #(.width(32)) register_5 (.D(esfkeyt_1_out_8), .en(not_10_out), .Q(out_12), .clk(and_1_out));  // open: clr

  // Notes on the sheet:
  //   L_0
  //   RoundFunc
  //   R_0
  //   need 16lsb
endmodule

module shift7 (
  input  [31:0] in_1,
  output [31:0] out_2
);


  assign out_2 = {in_1[24:0], in_1[31:25]};
endmodule

module RoundFunction (
  input  [31:0] in_1,
  input  [31:0] in_2,
  output [31:0] out_3
);

  wire [3:0] xor_1_out_2, xor_1_out_3;
  wire [31:0] xor_1_out;

  S7 s7_1 (
    .a1(xor_1_out[31]), .a2(xor_1_out[30]), .a3(xor_1_out[29]), .a4(xor_1_out[28]), .b1(out_3[31]),
    .b2(out_3[23]), .b3(out_3[15]), .b4(out_3[7]));
  S6 s6_1 (
    .a1(xor_1_out[27]), .a2(xor_1_out[26]), .a3(xor_1_out[25]), .a4(xor_1_out[24]), .b1(out_3[30]),
    .b2(out_3[22]), .b3(out_3[14]), .b4(out_3[6]));
  S5 s5_1 (
    .a1(xor_1_out_3[3]), .a2(xor_1_out_3[2]), .a3(xor_1_out_3[1]), .a4(xor_1_out_3[0]), .b1(out_3[29]),
    .b2(out_3[21]), .b3(out_3[13]), .b4(out_3[5]));
  S4 s4_1 (
    .a1(xor_1_out_2[3]), .a2(xor_1_out_2[2]), .a3(xor_1_out_2[1]), .a4(xor_1_out_2[0]), .b1(out_3[28]),
    .b2(out_3[20]), .b3(out_3[12]), .b4(out_3[4]));
  assign {xor_1_out[31:24], xor_1_out_3, xor_1_out_2, xor_1_out[15:0]} = in_1 ^ in_2;  // XOR_Gate xor_1, 32 bits wide
  S3 s3_1 (
    .a1(xor_1_out[15]), .a2(xor_1_out[14]), .a3(xor_1_out[13]), .a4(xor_1_out[12]), .b1(out_3[27]),
    .b2(out_3[19]), .b3(out_3[11]), .b4(out_3[3]));
  S2 s2_1 (
    .a1(xor_1_out[11]), .a2(xor_1_out[10]), .a3(xor_1_out[9]), .a4(xor_1_out[8]), .b1(out_3[26]),
    .b2(out_3[18]), .b3(out_3[10]), .b4(out_3[2]));
  S1 s1_1 (
    .in_1(xor_1_out[7]), .in_2(xor_1_out[6]), .in_3(xor_1_out[5]), .in_4(xor_1_out[4]), .out_5(out_3[25]),
    .out_6(out_3[17]), .out_7(out_3[9]), .out_8(out_3[1]));
  S0 s0_1 (
    .in_1(xor_1_out[3]), .in_2(xor_1_out[2]), .in_3(xor_1_out[1]), .in_4(xor_1_out[0]), .out_5(out_3[24]),
    .out_6(out_3[16]), .out_7(out_3[8]), .out_8(out_3[0]));

  // Notes on the sheet:
  //   serpent S boxes
  //   permutations
endmodule

module S0 (
  input  in_1,
  input  in_2,
  input  in_3,
  input  in_4,
  output out_5,
  output out_6,
  output out_7,
  output out_8
);

  wire and_1_out, and_2_out, and_3_out, and_4_out, and_5_out, and_6_out, and_7_out, and_8_out, and_9_out,
       and_10_out, and_11_out, and_12_out, and_13_out, and_14_out, and_15_out, and_16_out, and_17_out,
       and_18_out, and_19_out, not_1_out, not_2_out, not_3_out, not_4_out, not_5_out, not_6_out, not_7_out,
       not_8_out, not_9_out, not_10_out, not_11_out, not_12_out, not_13_out;

  not not_1 (not_1_out, in_1);
  not not_2 (not_2_out, in_2);
  not not_3 (not_3_out, in_3);
  not not_4 (not_4_out, in_4);
  and and_1 (and_1_out, in_1, in_2, in_3, in_4);
  and and_2 (and_2_out, not_2_out, not_3_out, in_4);
  and and_3 (and_3_out, in_4, in_3, in_2);
  and and_4 (and_4_out, not_2_out, not_3_out, in_1);
  and and_5 (and_5_out, in_2, in_3, in_1);
  or or_1 (out_5, and_2_out, and_3_out, and_4_out, and_5_out, and_6_out, and_8_out);
  and and_6 (and_6_out, not_1_out, not_2_out, in_3, not_4_out);
  and and_7 (and_7_out, not_1_out, in_3, not_4_out);
  and and_8 (and_8_out, in_2, not_1_out, not_3_out, not_4_out);
  and and_9 (and_9_out, in_3, not_4_out, not_2_out);
  or or_2 (out_6, and_7_out, and_9_out, and_4_out, and_10_out, and_11_out, and_1_out);
  and and_10 (and_10_out, in_1, not_4_out, not_3_out);
  and and_11 (and_11_out, in_2, in_4, not_1_out, not_3_out);
  and and_12 (and_12_out, not_3_out, not_4_out);
  not not_5 (not_5_out, not_2_out);
  and and_13 (and_13_out, not_1_out, not_2_out, not_4_out);
  not not_6 (not_6_out, not_1_out);
  not not_7 (not_7_out, not_4_out);
  not not_8 (not_8_out, not_3_out);
  and and_14 (and_14_out, not_1_out, not_5_out, not_7_out);
  and and_15 (and_15_out, not_2_out, not_6_out, not_8_out, not_9_out);
  or or_3 (out_7, and_12_out, and_13_out, and_14_out, and_15_out);
  not not_9 (not_9_out, not_4_out);
  not not_10 (not_10_out, not_3_out);
  and and_16 (and_16_out, not_1_out, not_10_out);
  and and_17 (and_17_out, not_1_out, not_2_out, not_4_out);
  or or_4 (out_8, and_16_out, and_17_out, and_18_out, and_19_out);
  not not_11 (not_11_out, not_2_out);
  not not_12 (not_12_out, not_1_out);
  and and_18 (and_18_out, not_4_out, not_11_out, not_12_out);
  and and_19 (and_19_out, not_12_out, not_2_out, not_3_out, not_13_out);
  not not_13 (not_13_out, not_4_out);
endmodule

module S1 (
  input  in_1,
  input  in_2,
  input  in_3,
  input  in_4,
  output out_5,
  output out_6,
  output out_7,
  output out_8
);

  wire and_1_out, and_2_out, and_3_out, and_4_out, and_5_out, and_6_out, and_7_out, and_8_out, and_9_out,
       and_10_out, and_11_out, and_12_out, and_13_out, and_14_out, and_15_out, and_16_out, and_17_out,
       and_18_out, and_19_out, and_20_out, and_21_out, not_1_out, not_2_out, not_3_out, not_4_out, not_5_out,
       not_6_out, not_7_out, not_8_out, not_9_out, not_10_out, not_11_out, not_12_out, not_13_out,
       not_14_out, not_15_out, not_16_out, not_17_out, not_18_out, not_19_out, not_20_out, not_21_out,
       not_22_out, not_23_out, not_24_out, not_25_out, not_26_out, not_27_out, not_28_out;

  not not_1 (not_1_out, in_2);
  not not_2 (not_2_out, in_3);
  not not_3 (not_3_out, in_2);
  not not_4 (not_4_out, in_1);
  not not_5 (not_5_out, in_2);
  not not_6 (not_6_out, in_3);
  not not_7 (not_7_out, in_4);
  not not_8 (not_8_out, in_1);
  not not_9 (not_9_out, in_2);
  not not_10 (not_10_out, in_3);
  not not_11 (not_11_out, in_4);
  not not_12 (not_12_out, in_2);
  not not_13 (not_13_out, in_1);
  not not_14 (not_14_out, in_1);
  not not_15 (not_15_out, in_3);
  not not_16 (not_16_out, in_4);
  and and_1 (and_1_out, not_8_out, not_9_out, not_10_out);
  and and_2 (and_2_out, not_8_out, not_10_out, not_11_out);
  and and_3 (and_3_out, not_10_out, in_1, in_4);
  and and_4 (and_4_out, in_1, not_12_out, in_3);
  and and_5 (and_5_out, not_13_out, in_2, in_3, in_4);
  and and_6 (and_6_out, not_14_out, not_1_out, not_15_out);
  and and_7 (and_7_out, not_14_out, not_1_out, in_4);
  and and_8 (and_8_out, in_1, in_2, not_2_out);
  and and_9 (and_9_out, in_1, in_3, not_3_out, not_16_out);
  and and_10 (and_10_out, in_2, in_1, in_4);
  and and_11 (and_11_out, not_14_out, in_2, in_3, not_16_out);
  or or_1 (out_5, and_1_out, and_2_out, and_3_out, and_4_out, and_5_out);
  or or_2 (out_6, and_11_out, and_6_out, and_7_out, and_8_out, and_9_out, and_10_out);
  not not_17 (not_17_out, not_7_out);
  not not_18 (not_18_out, not_6_out);
  and and_12 (and_12_out, not_17_out, not_4_out, not_18_out);
  not not_19 (not_19_out, not_6_out);
  and and_13 (and_13_out, not_5_out, not_19_out, not_7_out);
  and and_14 (and_14_out, not_5_out, not_4_out, not_7_out);
  or or_3 (out_7, and_12_out, and_13_out, and_14_out, and_16_out, and_15_out);
  not not_20 (not_20_out, not_5_out);
  not not_21 (not_21_out, not_7_out);
  not not_22 (not_22_out, not_4_out);
  and and_15 (and_15_out, not_22_out, not_7_out, not_20_out);
  and and_16 (and_16_out, not_6_out, not_5_out, not_22_out, not_21_out);
  and and_17 (and_17_out, not_4_out, not_6_out, not_7_out);
  not not_23 (not_23_out, not_5_out);
  and and_18 (and_18_out, not_5_out, not_7_out, not_6_out);
  not not_24 (not_24_out, not_6_out);
  not not_25 (not_25_out, not_4_out);
  and and_19 (and_19_out, not_23_out, not_24_out, not_7_out);
  or or_4 (out_8, and_17_out, and_18_out, and_19_out, and_20_out, and_21_out);
  not not_26 (not_26_out, not_7_out);
  and and_20 (and_20_out, not_25_out, not_6_out, not_26_out);
  and and_21 (and_21_out, not_4_out, not_5_out, not_28_out, not_27_out);
  not not_27 (not_27_out, not_7_out);
  not not_28 (not_28_out, not_6_out);
endmodule

module S2 (
  input  a1,
  input  a2,
  input  a3,
  input  a4,
  output b1,
  output b2,
  output b3,
  output b4
);

  wire and_1_out, and_2_out, and_3_out, and_4_out, and_5_out, and_6_out, and_7_out, and_8_out, and_9_out,
       and_10_out, and_11_out, and_12_out, and_13_out, and_14_out, and_15_out, and_16_out, and_17_out,
       and_18_out, and_19_out, and_20_out, and_21_out, and_22_out, not_1_out, not_2_out, not_3_out,
       not_4_out, not_5_out, not_6_out, not_7_out, not_8_out, not_9_out, not_10_out, not_11_out, not_12_out,
       not_13_out, not_14_out, not_15_out, not_16_out, not_17_out, not_18_out, not_19_out, not_20_out,
       not_21_out, not_22_out, not_23_out, not_24_out, not_25_out, not_26_out, not_27_out, not_28_out,
       not_29_out, not_30_out, not_31_out, not_32_out, not_33_out, not_34_out, not_35_out;

  not not_1 (not_1_out, a2);
  and and_1 (and_1_out, not_1_out, not_2_out, not_3_out);
  not not_2 (not_2_out, a3);
  not not_3 (not_3_out, a4);
  not not_4 (not_4_out, a1);
  and and_2 (and_2_out, not_4_out, a3, a4);
  and and_3 (and_3_out, a2, not_5_out, a4);
  not not_5 (not_5_out, a3);
  not not_6 (not_6_out, a1);
  and and_4 (and_4_out, not_6_out, a2, a3);
  not not_7 (not_7_out, a2);
  and and_5 (and_5_out, a1, not_7_out, not_8_out);
  not not_8 (not_8_out, a4);
  not not_9 (not_9_out, a1);
  not not_10 (not_10_out, a3);
  and and_6 (and_6_out, not_9_out, not_10_out, a4);
  not not_11 (not_11_out, a2);
  and and_7 (and_7_out, not_11_out, a3, not_12_out);
  not not_12 (not_12_out, a4);
  not not_13 (not_13_out, a1);
  and and_8 (and_8_out, not_13_out, a2, a4);
  and and_9 (and_9_out, a1, not_14_out, not_15_out);
  not not_14 (not_14_out, a2);
  not not_15 (not_15_out, a4);
  not not_16 (not_16_out, a2);
  and and_10 (and_10_out, a1, not_16_out, a3);
  and and_11 (and_11_out, a1, a3, not_17_out);
  not not_17 (not_17_out, a4);
  not not_18 (not_18_out, a1);
  not not_19 (not_19_out, a2);
  not not_20 (not_20_out, a3);
  not not_21 (not_21_out, a2);
  not not_22 (not_22_out, a4);
  not not_23 (not_23_out, a1);
  not not_24 (not_24_out, a4);
  not not_25 (not_25_out, a1);
  not not_26 (not_26_out, a1);
  not not_27 (not_27_out, a2);
  not not_28 (not_28_out, a1);
  not not_29 (not_29_out, a1);
  not not_30 (not_30_out, a3);
  not not_31 (not_31_out, a4);
  not not_32 (not_32_out, a2);
  not not_33 (not_33_out, a3);
  not not_34 (not_34_out, a3);
  not not_35 (not_35_out, a4);
  or or_1 (b1, and_1_out, and_2_out, and_3_out, and_4_out, and_5_out);
  and and_12 (and_12_out, not_18_out, not_19_out, not_20_out, a4);
  and and_13 (and_13_out, not_21_out, a3, not_22_out);
  and and_14 (and_14_out, not_23_out, a2, not_24_out);
  and and_15 (and_15_out, not_25_out, a2, a3);
  and and_16 (and_16_out, a1, a2, a4);
  and and_17 (and_17_out, not_26_out, not_27_out, a3);
  and and_18 (and_18_out, not_28_out, a3, a4);
  and and_19 (and_19_out, not_29_out, a2, not_30_out, not_31_out);
  and and_20 (and_20_out, a1, not_32_out, not_33_out);
  and and_21 (and_21_out, a1, not_34_out, a4);
  and and_22 (and_22_out, a1, a2, a3, not_35_out);
  or or_2 (b2, and_6_out, and_7_out, and_8_out, and_9_out, and_10_out, and_11_out);
  or or_3 (b3, and_12_out, and_13_out, and_14_out, and_15_out, and_16_out);
  or or_4 (b4, and_17_out, and_18_out, and_19_out, and_20_out, and_21_out, and_22_out);
endmodule

module S3 (
  input  a1,
  input  a2,
  input  a3,
  input  a4,
  output b1,
  output b2,
  output b3,
  output b4
);

  wire and_1_out, and_2_out, and_3_out, and_4_out, and_5_out, and_6_out, and_7_out, and_8_out, and_9_out,
       and_10_out, and_11_out, and_12_out, and_13_out, and_14_out, and_15_out, and_16_out, and_17_out,
       and_18_out, and_19_out, and_20_out, and_21_out, not_1_out, not_2_out, not_3_out, not_4_out, not_5_out,
       not_6_out, not_7_out, not_8_out, not_9_out, not_10_out, not_11_out, not_12_out, not_13_out,
       not_14_out, not_15_out, not_16_out, not_17_out, not_18_out, not_19_out, not_20_out, not_21_out,
       not_22_out, not_23_out, not_24_out, not_25_out, not_26_out, not_27_out, not_28_out, not_29_out,
       not_30_out, not_31_out, not_32_out;

  not not_1 (not_1_out, a1);
  and and_1 (and_1_out, not_1_out, not_2_out, a4);
  not not_2 (not_2_out, a2);
  not not_3 (not_3_out, a1);
  not not_4 (not_4_out, a2);
  and and_2 (and_2_out, not_3_out, not_4_out, a3);
  not not_5 (not_5_out, a1);
  and and_3 (and_3_out, not_5_out, a2, not_6_out);
  not not_6 (not_6_out, a3);
  and and_4 (and_4_out, a1, not_7_out, not_8_out);
  not not_7 (not_7_out, a3);
  not not_8 (not_8_out, a4);
  and and_5 (and_5_out, a1, a2, a3, a4);
  not not_9 (not_9_out, a1);
  not not_10 (not_10_out, a2);
  not not_11 (not_11_out, a3);
  not not_12 (not_12_out, a1);
  not not_13 (not_13_out, a4);
  not not_14 (not_14_out, a4);
  not not_15 (not_15_out, a2);
  not not_16 (not_16_out, a3);
  not not_17 (not_17_out, a4);
  not not_18 (not_18_out, a1);
  not not_19 (not_19_out, a2);
  not not_20 (not_20_out, a3);
  not not_21 (not_21_out, a2);
  not not_22 (not_22_out, a4);
  not not_23 (not_23_out, a1);
  not not_24 (not_24_out, a3);
  not not_25 (not_25_out, a3);
  not not_26 (not_26_out, a1);
  not not_27 (not_27_out, a2);
  not not_28 (not_28_out, a4);
  not not_29 (not_29_out, a1);
  not not_30 (not_30_out, a2);
  not not_31 (not_31_out, a3);
  not not_32 (not_32_out, a4);
  or or_1 (b1, and_1_out, and_2_out, and_3_out, and_4_out, and_5_out);
  and and_6 (and_6_out, not_9_out, not_10_out, not_11_out, a4);
  and and_7 (and_7_out, not_12_out, a2, not_13_out);
  and and_8 (and_8_out, a2, a3, not_14_out);
  and and_9 (and_9_out, a1, not_15_out, not_16_out, not_17_out);
  and and_10 (and_10_out, a1, a3, a4);
  and and_11 (and_11_out, a1, a2, a4);
  and and_12 (and_12_out, not_18_out, not_19_out, not_20_out, a4);
  and and_13 (and_13_out, not_21_out, a3, not_22_out);
  and and_14 (and_14_out, not_23_out, a2, a3);
  and and_15 (and_15_out, a1, a2, not_24_out);
  and and_16 (and_16_out, a1, a2, a4);
  and and_17 (and_17_out, not_25_out, a4);
  and and_18 (and_18_out, not_26_out, not_27_out, a3, not_28_out);
  and and_19 (and_19_out, not_29_out, a2, a4);
  and and_20 (and_20_out, a1, not_30_out, not_31_out);
  and and_21 (and_21_out, a1, a2, a3, not_32_out);
  or or_2 (b2, and_6_out, and_7_out, and_8_out, and_9_out, and_10_out, and_11_out);
  or or_3 (b3, and_12_out, and_13_out, and_14_out, and_15_out, and_16_out);
  or or_4 (b4, and_17_out, and_18_out, and_19_out, and_20_out, and_21_out);
endmodule

module S4 (
  input  a1,
  input  a2,
  input  a3,
  input  a4,
  output b1,
  output b2,
  output b3,
  output b4
);

  wire and_1_out, and_2_out, and_3_out, and_4_out, and_5_out, and_6_out, and_7_out, and_8_out, and_9_out,
       and_10_out, and_11_out, and_12_out, and_13_out, and_14_out, and_15_out, and_16_out, and_17_out,
       and_18_out, and_19_out, and_20_out, and_21_out, and_22_out, not_1_out, not_2_out, not_3_out,
       not_4_out, not_5_out, not_6_out, not_7_out, not_8_out, not_9_out, not_10_out, not_11_out, not_12_out,
       not_13_out, not_14_out, not_15_out, not_16_out, not_17_out, not_18_out, not_19_out, not_20_out,
       not_21_out, not_22_out, not_23_out, not_24_out, not_25_out, not_26_out, not_27_out, not_28_out,
       not_29_out, not_30_out, not_31_out, not_32_out, not_33_out;

  not not_1 (not_1_out, a1);
  not not_2 (not_2_out, a2);
  not not_3 (not_3_out, a3);
  not not_4 (not_4_out, a1);
  not not_5 (not_5_out, a4);
  not not_6 (not_6_out, a3);
  not not_7 (not_7_out, a4);
  not not_8 (not_8_out, a3);
  not not_9 (not_9_out, a2);
  not not_10 (not_10_out, a3);
  not not_11 (not_11_out, a1);
  not not_12 (not_12_out, a3);
  not not_13 (not_13_out, a4);
  not not_14 (not_14_out, a3);
  not not_15 (not_15_out, a4);
  not not_16 (not_16_out, a1);
  not not_17 (not_17_out, a2);
  not not_18 (not_18_out, a2);
  not not_19 (not_19_out, a1);
  not not_20 (not_20_out, a4);
  not not_21 (not_21_out, a2);
  not not_22 (not_22_out, a3);
  not not_23 (not_23_out, a4);
  not not_24 (not_24_out, a3);
  not not_25 (not_25_out, a1);
  and and_1 (and_1_out, not_25_out, not_26_out, not_27_out);
  not not_26 (not_26_out, a2);
  not not_27 (not_27_out, a3);
  not not_28 (not_28_out, a1);
  not not_29 (not_29_out, a2);
  and and_2 (and_2_out, not_28_out, not_29_out, a4);
  not not_30 (not_30_out, a2);
  not not_31 (not_31_out, a3);
  and and_3 (and_3_out, not_30_out, not_31_out, a4);
  and and_4 (and_4_out, a2, a3, not_32_out);
  not not_32 (not_32_out, a4);
  and and_5 (and_5_out, a1, a2, not_33_out);
  not not_33 (not_33_out, a4);
  and and_6 (and_6_out, a1, a2, a3);
  and and_7 (and_7_out, not_1_out, not_2_out, not_3_out, a4);
  and and_8 (and_8_out, not_4_out, a3, not_5_out);
  and and_9 (and_9_out, a2, not_6_out, not_7_out);
  and and_10 (and_10_out, a1, a3, a4);
  and and_11 (and_11_out, a1, a2, not_8_out);
  and and_12 (and_12_out, not_9_out, not_10_out, a4);
  and and_13 (and_13_out, not_11_out, a2, not_12_out, not_13_out);
  and and_14 (and_14_out, a2, a3, a4);
  and and_15 (and_15_out, a1, not_14_out, a4);
  and and_16 (and_16_out, a1, a3, not_15_out);
  and and_17 (and_17_out, not_16_out, not_17_out, a4);
  and and_18 (and_18_out, not_18_out, a3, a4);
  and and_19 (and_19_out, not_19_out, a2, a3);
  and and_20 (and_20_out, a2, a3, not_20_out);
  and and_21 (and_21_out, a1, not_21_out, not_22_out, not_23_out);
  and and_22 (and_22_out, a1, a2, not_24_out, a4);
  or or_1 (b1, and_7_out, and_8_out, and_9_out, and_10_out, and_11_out);
  or or_2 (b2, and_12_out, and_13_out, and_14_out, and_15_out, and_16_out);
  or or_3 (b3, and_17_out, and_18_out, and_19_out, and_20_out, and_21_out, and_22_out);
  or or_4 (b4, and_1_out, and_2_out, and_3_out, and_4_out, and_5_out, and_6_out);
endmodule

module S5 (
  input  a1,
  input  a2,
  input  a3,
  input  a4,
  output b1,
  output b2,
  output b3,
  output b4
);

  wire and_1_out, and_2_out, and_3_out, and_4_out, and_5_out, and_6_out, and_7_out, and_8_out, and_9_out,
       and_10_out, and_11_out, and_12_out, and_13_out, and_14_out, and_15_out, and_16_out, and_17_out,
       and_18_out, and_19_out, and_20_out, and_21_out, and_22_out, not_1_out, not_2_out, not_3_out,
       not_4_out, not_5_out, not_6_out, not_7_out, not_8_out, not_9_out, not_10_out, not_11_out, not_12_out,
       not_13_out, not_14_out, not_15_out, not_16_out, not_17_out, not_18_out, not_19_out, not_20_out,
       not_21_out, not_22_out, not_23_out, not_24_out, not_25_out, not_26_out, not_27_out, not_28_out,
       not_29_out, not_30_out, not_31_out, not_32_out, not_33_out, not_34_out, not_35_out, not_36_out;

  not not_1 (not_1_out, a1);
  not not_2 (not_2_out, a2);
  not not_3 (not_3_out, a3);
  not not_4 (not_4_out, a4);
  not not_5 (not_5_out, a1);
  not not_6 (not_6_out, a1);
  not not_7 (not_7_out, a1);
  not not_8 (not_8_out, a2);
  not not_9 (not_9_out, a3);
  not not_10 (not_10_out, a4);
  not not_11 (not_11_out, a1);
  not not_12 (not_12_out, a2);
  not not_13 (not_13_out, a3);
  not not_14 (not_14_out, a1);
  not not_15 (not_15_out, a3);
  not not_16 (not_16_out, a4);
  not not_17 (not_17_out, a1);
  not not_18 (not_18_out, a4);
  not not_19 (not_19_out, a3);
  not not_20 (not_20_out, a1);
  not not_21 (not_21_out, a2);
  and and_1 (and_1_out, not_20_out, not_21_out, not_22_out);
  not not_22 (not_22_out, a4);
  not not_23 (not_23_out, a1);
  not not_24 (not_24_out, a2);
  and and_2 (and_2_out, not_23_out, not_24_out, a3);
  not not_25 (not_25_out, a3);
  and and_3 (and_3_out, a2, not_25_out, a4);
  not not_26 (not_26_out, a3);
  and and_4 (and_4_out, a1, not_26_out, a4);
  and and_5 (and_5_out, a1, a3, not_27_out);
  not not_27 (not_27_out, a4);
  not not_28 (not_28_out, a1);
  and and_6 (and_6_out, not_28_out, not_29_out, not_30_out);
  not not_29 (not_29_out, a2);
  not not_30 (not_30_out, a3);
  not not_31 (not_31_out, a1);
  not not_32 (not_32_out, a2);
  and and_7 (and_7_out, not_31_out, not_32_out, a4);
  not not_33 (not_33_out, a2);
  and and_8 (and_8_out, not_33_out, not_34_out, a4);
  not not_34 (not_34_out, a3);
  and and_9 (and_9_out, a2, a3, not_35_out);
  not not_35 (not_35_out, a4);
  and and_10 (and_10_out, a1, a2, not_36_out);
  not not_36 (not_36_out, a4);
  and and_11 (and_11_out, a1, a2, a3);
  and and_12 (and_12_out, not_1_out, not_2_out, not_3_out, not_4_out);
  and and_13 (and_13_out, not_5_out, a3, a4);
  and and_14 (and_14_out, not_6_out, a2, a4);
  and and_15 (and_15_out, not_7_out, a2, a3);
  and and_16 (and_16_out, a1, not_8_out, a3);
  and and_17 (and_17_out, a1, a2, not_9_out, not_10_out);
  and and_18 (and_18_out, not_11_out, not_12_out, not_13_out);
  and and_19 (and_19_out, not_14_out, not_15_out, not_16_out);
  and and_20 (and_20_out, not_17_out, a2, a3, a4);
  and and_21 (and_21_out, a1, a3, not_18_out);
  and and_22 (and_22_out, a1, a2, not_19_out);
  or or_1 (b3, and_1_out, and_2_out, and_3_out, and_4_out, and_5_out);
  or or_2 (b1, and_12_out, and_13_out, and_14_out, and_15_out, and_16_out, and_17_out);
  or or_3 (b2, and_18_out, and_19_out, and_20_out, and_21_out, and_22_out);
  or or_4 (b4, and_6_out, and_7_out, and_8_out, and_9_out, and_10_out, and_11_out);
endmodule

module S6 (
  input  a1,
  input  a2,
  input  a3,
  input  a4,
  output b1,
  output b2,
  output b3,
  output b4
);

  wire and_1_out, and_2_out, and_3_out, and_4_out, and_5_out, and_6_out, and_7_out, and_8_out, and_9_out,
       and_10_out, and_11_out, and_12_out, and_13_out, and_14_out, and_15_out, and_16_out, and_17_out,
       and_18_out, and_19_out, and_20_out, and_21_out, and_22_out, not_1_out, not_2_out, not_3_out,
       not_4_out, not_5_out, not_6_out, not_7_out, not_8_out, not_9_out, not_10_out, not_11_out, not_12_out,
       not_13_out, not_14_out, not_15_out, not_16_out, not_17_out, not_18_out, not_19_out, not_20_out,
       not_21_out, not_22_out, not_23_out, not_24_out, not_25_out, not_26_out, not_27_out, not_28_out,
       not_29_out, not_30_out, not_31_out, not_32_out, not_33_out, not_34_out, not_35_out, not_36_out,
       not_37_out, not_38_out;

  not not_1 (not_1_out, a1);
  not not_2 (not_2_out, a2);
  not not_3 (not_3_out, a4);
  not not_4 (not_4_out, a3);
  not not_5 (not_5_out, a4);
  not not_6 (not_6_out, a1);
  not not_7 (not_7_out, a2);
  not not_8 (not_8_out, a3);
  not not_9 (not_9_out, a2);
  not not_10 (not_10_out, a4);
  not not_11 (not_11_out, a1);
  not not_12 (not_12_out, a2);
  not not_13 (not_13_out, a4);
  not not_14 (not_14_out, a1);
  not not_15 (not_15_out, a4);
  not not_16 (not_16_out, a2);
  not not_17 (not_17_out, a1);
  not not_18 (not_18_out, a3);
  not not_19 (not_19_out, a3);
  not not_20 (not_20_out, a4);
  not not_21 (not_21_out, a1);
  not not_22 (not_22_out, a2);
  not not_23 (not_23_out, a3);
  not not_24 (not_24_out, a2);
  not not_25 (not_25_out, a3);
  not not_26 (not_26_out, a4);
  not not_27 (not_27_out, a1);
  not not_28 (not_28_out, a4);
  not not_29 (not_29_out, a2);
  not not_30 (not_30_out, a3);
  not not_31 (not_31_out, a1);
  not not_32 (not_32_out, a2);
  not not_33 (not_33_out, a3);
  not not_34 (not_34_out, a4);
  not not_35 (not_35_out, a1);
  not not_36 (not_36_out, a2);
  not not_37 (not_37_out, a2);
  not not_38 (not_38_out, a3);
  and and_1 (and_1_out, not_1_out, not_2_out, a3, not_3_out);
  and and_2 (and_2_out, a2, not_4_out, not_5_out);
  and and_3 (and_3_out, not_6_out, a2, a3, a4);
  and and_4 (and_4_out, a1, not_7_out, not_8_out);
  and and_5 (and_5_out, a1, not_9_out, a4);
  and and_6 (and_6_out, a1, a2, not_10_out);
  and and_7 (and_7_out, not_11_out, not_12_out, not_13_out);
  and and_8 (and_8_out, not_14_out, a3, not_15_out);
  and and_9 (and_9_out, not_16_out, a3, a4);
  and and_10 (and_10_out, not_17_out, a2, not_18_out, a4);
  and and_11 (and_11_out, a1, not_19_out, not_20_out);
  and and_12 (and_12_out, not_21_out, not_22_out, not_23_out);
  and and_13 (and_13_out, not_24_out, not_25_out, not_26_out);
  and and_14 (and_14_out, not_27_out, a2, a3);
  and and_15 (and_15_out, a2, a3, not_28_out);
  and and_16 (and_16_out, a1, not_29_out, a3, a4);
  and and_17 (and_17_out, a1, a2, not_30_out, a4);
  and and_18 (and_18_out, not_31_out, not_32_out, not_33_out, not_34_out);
  and and_19 (and_19_out, not_35_out, a3, a4);
  and and_20 (and_20_out, a1, not_36_out, a4);
  and and_21 (and_21_out, a1, not_37_out, a3);
  and and_22 (and_22_out, a1, a2, not_38_out);
  or or_1 (b1, and_1_out, and_2_out, and_3_out, and_4_out, and_5_out, and_6_out);
  or or_2 (b2, and_7_out, and_8_out, and_9_out, and_10_out, and_11_out);
  or or_3 (b3, and_12_out, and_13_out, and_14_out, and_15_out, and_16_out, and_17_out);
  or or_4 (b4, and_18_out, and_19_out, and_20_out, and_21_out, and_22_out);
endmodule

module S7 (
  input  a1,
  input  a2,
  input  a3,
  input  a4,
  output b1,
  output b2,
  output b3,
  output b4
);

  wire and_1_out, and_2_out, and_3_out, and_4_out, and_5_out, and_6_out, and_7_out, and_8_out, and_9_out,
       and_10_out, and_11_out, and_12_out, and_13_out, and_14_out, and_15_out, and_16_out, and_17_out,
       and_18_out, and_19_out, and_20_out, and_21_out, and_22_out, not_1_out, not_2_out, not_3_out,
       not_4_out, not_5_out, not_6_out, not_7_out, not_8_out, not_9_out, not_10_out, not_11_out, not_12_out,
       not_13_out, not_14_out, not_15_out, not_16_out, not_17_out, not_18_out, not_19_out, not_20_out,
       not_21_out, not_22_out, not_23_out, not_24_out, not_25_out, not_26_out, not_27_out, not_28_out,
       not_29_out, not_30_out, not_31_out, not_32_out, not_33_out, not_34_out, not_35_out, not_36_out,
       not_37_out;

  not not_1 (not_1_out, a1);
  not not_2 (not_2_out, a3);
  and and_1 (and_1_out, not_1_out, not_2_out, a4);
  not not_3 (not_3_out, a2);
  and and_2 (and_2_out, not_3_out, a3, not_4_out);
  not not_4 (not_4_out, a4);
  and and_3 (and_3_out, a2, not_5_out, not_6_out);
  not not_5 (not_5_out, a3);
  not not_6 (not_6_out, a4);
  not not_7 (not_7_out, a1);
  and and_4 (and_4_out, not_7_out, a2, a4);
  not not_8 (not_8_out, a2);
  and and_5 (and_5_out, a1, not_8_out, a3);
  not not_9 (not_9_out, a2);
  not not_10 (not_10_out, a3);
  not not_11 (not_11_out, a2);
  not not_12 (not_12_out, a4);
  not not_13 (not_13_out, a1);
  not not_14 (not_14_out, a3);
  not not_15 (not_15_out, a4);
  not not_16 (not_16_out, a2);
  not not_17 (not_17_out, a3);
  not not_18 (not_18_out, a1);
  not not_19 (not_19_out, a4);
  not not_20 (not_20_out, a1);
  not not_21 (not_21_out, a4);
  not not_22 (not_22_out, a1);
  not not_23 (not_23_out, a2);
  not not_24 (not_24_out, a3);
  not not_25 (not_25_out, a4);
  not not_26 (not_26_out, a1);
  not not_27 (not_27_out, a2);
  not not_28 (not_28_out, a3);
  not not_29 (not_29_out, a1);
  not not_30 (not_30_out, a2);
  not not_31 (not_31_out, a4);
  not not_32 (not_32_out, a2);
  not not_33 (not_33_out, a3);
  not not_34 (not_34_out, a4);
  not not_35 (not_35_out, a1);
  not not_36 (not_36_out, a3);
  not not_37 (not_37_out, a4);
  or or_1 (b1, and_1_out, and_2_out, and_3_out, and_4_out, and_5_out);
  and and_6 (and_6_out, not_9_out, not_10_out, a4);
  and and_7 (and_7_out, not_11_out, a3, not_12_out);
  and and_8 (and_8_out, not_13_out, a2, not_14_out, not_15_out);
  and and_9 (and_9_out, a1, not_16_out, not_17_out);
  and and_10 (and_10_out, a1, a2, a3);
  and and_11 (and_11_out, not_18_out, a3, not_19_out);
  and and_12 (and_12_out, not_20_out, a2, not_21_out);
  and and_13 (and_13_out, not_22_out, a2, a3);
  and and_14 (and_14_out, a1, not_23_out, not_24_out, not_25_out);
  and and_15 (and_15_out, a1, a3, a4);
  and and_16 (and_16_out, a1, a2, a4);
  and and_17 (and_17_out, not_26_out, not_27_out, not_28_out);
  and and_18 (and_18_out, not_29_out, not_30_out, not_31_out);
  and and_19 (and_19_out, not_32_out, not_33_out, not_34_out);
  and and_20 (and_20_out, not_35_out, a2, a3, a4);
  and and_21 (and_21_out, a1, a2, not_36_out);
  and and_22 (and_22_out, a1, a2, not_37_out);
  or or_2 (b2, and_6_out, and_7_out, and_8_out, and_9_out, and_10_out);
  or or_3 (b3, and_11_out, and_12_out, and_13_out, and_14_out, and_15_out, and_16_out);
  or or_4 (b4, and_17_out, and_18_out, and_19_out, and_20_out, and_21_out, and_22_out);
endmodule

module esfKeyT (
  input  [15:0] in_1,
  input  in_2,
  input  [31:0] in_3,
  input  [4:0] counter,
  input  [31:0] in_5,
  output [15:0] out_6,
  output [31:0] out_7,
  output [31:0] out_8
);

  wire [3:0] not_1_out;
  wire [31:0] shifter_1_out, shifter_2_out;

  not not_1 (not_1_out[0], in_2);
  not not_2 (not_1_out[2], in_2);
  not not_3 (not_1_out[3], in_2);
  Shifter #(.width(32)) shifter_1 (
    .in(in_5), .\dist ({in_2, not_1_out[3:2], in_2, not_1_out[0]}),
    .out({shifter_1_out[31:24], out_8[23:13], shifter_1_out[12:0]}));
  S0 s0_1 (
    .in_1(shifter_1_out[31]), .in_2(shifter_1_out[30]), .in_3(shifter_1_out[29]), .in_4(shifter_1_out[28]),
    .out_5(out_8[31]), .out_6(out_8[30]), .out_7(out_8[29]), .out_8(out_8[28]));
  S0 s0_2 (
    .in_1(shifter_1_out[27]), .in_2(shifter_1_out[26]), .in_3(shifter_1_out[25]), .in_4(shifter_1_out[24]),
    .out_5(out_8[27]), .out_6(out_8[26]), .out_7(out_8[25]), .out_8(out_8[24]));
  Shifter #(.width(32)) shifter_2 (
    .in(in_3), .\dist ({in_2, not_1_out[3:2], in_2, not_1_out[0]}),
    .out({shifter_2_out[31:27], out_7[26:13], shifter_2_out[12:0]}));
  assign out_7[31:27] = shifter_2_out[31:27] ^ counter;  // XOR_Gate xor_1, 5 bits wide

  assign out_6 = {in_1[2:0], in_5[31:19]};
  assign out_7[12:0] = in_1[15:3];
  assign out_8[12:0] = in_3[31:19];
endmodule
