// Logisim project SPNet.circ as structural Verilog: 1 circuit, main circuit main
module main (
  input  [31:0] in_1,
  input  [31:0] in_2,
  output [31:0] out_3,
  output [31:0] out_4
);

  Sbox_main main_1 (
    .msb_to_lsb(in_2[31]), .in_2(in_2[30]), .in_3(in_2[29]), .in_4(in_2[28]), .out_5(out_3[31]),
    .out_6(out_3[15]), .out_7(out_4[31]), .out_8(out_4[15]));
  Sbox_main main_2 (
    .msb_to_lsb(in_2[27]), .in_2(in_2[26]), .in_3(in_2[25]), .in_4(in_2[24]), .out_5(out_3[30]),
    .out_6(out_3[14]), .out_7(out_4[30]), .out_8(out_4[14]));
  Sbox_main main_3 (
    .msb_to_lsb(in_2[23]), .in_2(in_2[22]), .in_3(in_2[21]), .in_4(in_2[20]), .out_5(out_3[29]),
    .out_6(out_3[13]), .out_7(out_4[29]), .out_8(out_4[13]));
  Sbox_main main_4 (
    .msb_to_lsb(in_2[19]), .in_2(in_2[18]), .in_3(in_2[17]), .in_4(in_2[16]), .out_5(out_3[28]),
    .out_6(out_3[12]), .out_7(out_4[28]), .out_8(out_4[12]));
  Sbox_main main_5 (
    .msb_to_lsb(in_2[15]), .in_2(in_2[14]), .in_3(in_2[13]), .in_4(in_2[12]), .out_5(out_3[27]),
    .out_6(out_3[11]), .out_7(out_4[27]), .out_8(out_4[11]));
  Sbox_main main_6 (
    .msb_to_lsb(in_2[11]), .in_2(in_2[10]), .in_3(in_2[9]), .in_4(in_2[8]), .out_5(out_3[26]),
    .out_6(out_3[10]), .out_7(out_4[26]), .out_8(out_4[10]));
  Sbox_main main_7 (
    .msb_to_lsb(in_2[7]), .in_2(in_2[6]), .in_3(in_2[5]), .in_4(in_2[4]), .out_5(out_3[25]),
    .out_6(out_3[9]), .out_7(out_4[25]), .out_8(out_4[9]));
  Sbox_main main_8 (
    .msb_to_lsb(in_2[3]), .in_2(in_2[2]), .in_3(in_2[1]), .in_4(in_2[0]), .out_5(out_3[24]),
    .out_6(out_3[8]), .out_7(out_4[24]), .out_8(out_4[8]));
  Sbox_main main_9 (
    .msb_to_lsb(in_1[31]), .in_2(in_1[30]), .in_3(in_1[29]), .in_4(in_1[28]), .out_5(out_3[23]),
    .out_6(out_3[7]), .out_7(out_4[23]), .out_8(out_4[7]));
  Sbox_main main_10 (
    .msb_to_lsb(in_1[27]), .in_2(in_1[26]), .in_3(in_1[25]), .in_4(in_1[24]), .out_5(out_3[22]),
    .out_6(out_3[6]), .out_7(out_4[22]), .out_8(out_4[6]));
  Sbox_main main_11 (
    .msb_to_lsb(in_1[23]), .in_2(in_1[22]), .in_3(in_1[21]), .in_4(in_1[20]), .out_5(out_3[21]),
    .out_6(out_3[5]), .out_7(out_4[21]), .out_8(out_4[5]));
  Sbox_main main_12 (
    .msb_to_lsb(in_1[19]), .in_2(in_1[18]), .in_3(in_1[17]), .in_4(in_1[16]), .out_5(out_3[20]),
    .out_6(out_3[4]), .out_7(out_4[20]), .out_8(out_4[4]));
  Sbox_main main_13 (
    .msb_to_lsb(in_1[15]), .in_2(in_1[14]), .in_3(in_1[13]), .in_4(in_1[12]), .out_5(out_3[19]),
    .out_6(out_3[3]), .out_7(out_4[19]), .out_8(out_4[3]));
  Sbox_main main_14 (
    .msb_to_lsb(in_1[11]), .in_2(in_1[10]), .in_3(in_1[9]), .in_4(in_1[8]), .out_5(out_3[18]),
    .out_6(out_3[2]), .out_7(out_4[18]), .out_8(out_4[2]));
  Sbox_main main_15 (
    .msb_to_lsb(in_1[7]), .in_2(in_1[6]), .in_3(in_1[5]), .in_4(in_1[4]), .out_5(out_3[17]),
    .out_6(out_3[1]), .out_7(out_4[17]), .out_8(out_4[1]));
  Sbox_main main_16 (
    .msb_to_lsb(in_1[3]), .in_2(in_1[2]), .in_3(in_1[1]), .in_4(in_1[0]), .out_5(out_3[16]),
    .out_6(out_3[0]), .out_7(out_4[16]), .out_8(out_4[0]));

  // Notes on the sheet:
  //   48
  //   48
  //   16
  //   32
  //   32
  //   0
  //   16
  //   16
  //   0
endmodule
