// Logisim project Sbox.circ as structural Verilog: 1 circuit, main circuit main
module main (
  input  msb_to_lsb,
  input  in_2,
  input  in_3,
  input  in_4,
  output out_5,
  output out_6,
  output out_7,
  output out_8
);

  wire and_1_out, and_2_out, and_3_out, and_4_out, and_5_out, and_6_out, and_7_out, and_8_out, and_9_out,
       and_10_out, and_11_out, and_12_out, and_13_out, and_14_out, and_15_out, and_16_out, and_17_out,
       and_18_out, and_19_out, and_20_out, and_21_out, not_1_out, not_2_out, not_3_out, not_4_out;

  not not_1 (not_1_out, msb_to_lsb);
  not not_2 (not_2_out, in_2);
  not not_3 (not_3_out, in_3);
  not not_4 (not_4_out, in_4);
  and and_1 (and_1_out, not_4_out, not_3_out, not_1_out);
  and and_2 (and_2_out, not_1_out, in_3, in_4);
  and and_3 (and_3_out, not_1_out, not_4_out, in_2);
  and and_4 (and_4_out, msb_to_lsb, not_2_out, in_4);
  and and_5 (and_5_out, msb_to_lsb, not_2_out, in_3);
  and and_6 (and_6_out, not_2_out, in_3, not_4_out);
  and and_7 (and_7_out, msb_to_lsb, in_2, not_3_out);
  and and_8 (and_8_out, in_2, in_3, in_4, not_1_out);
  and and_9 (and_9_out, not_1_out, not_2_out, in_3);
  and and_10 (and_10_out, not_1_out, in_3, not_4_out);
  and and_11 (and_11_out, not_2_out, in_3, not_4_out);
  and and_12 (and_12_out, msb_to_lsb, not_2_out, not_3_out);
  and and_13 (and_13_out, msb_to_lsb, in_2, in_4);
  and and_14 (and_14_out, not_1_out, not_2_out, in_4);
  and and_15 (and_15_out, not_1_out, in_3, in_4);
  and and_16 (and_16_out, msb_to_lsb, not_2_out, not_4_out);
  and and_17 (and_17_out, msb_to_lsb, in_3, not_4_out);
  and and_18 (and_18_out, not_1_out, not_2_out, not_3_out);
  or or_1 (out_5, and_1_out, and_2_out, and_3_out, and_4_out, and_5_out);
  and and_19 (and_19_out, and_3_out, not_3_out);
  and and_20 (and_20_out, and_7_out, in_4);
  and and_21 (and_21_out, not_2_out, not_3_out, in_4);
  or or_2 (out_6, and_21_out, and_18_out, and_6_out, and_7_out, and_8_out);
  or or_3 (out_7, and_9_out, and_10_out, and_11_out, and_12_out, and_13_out);
  or or_4 (out_8, and_14_out, and_15_out, and_16_out, and_19_out, and_17_out, and_20_out);

  // Notes on the sheet:
  //   gives B1
  //   gives B3
  //   gives B2
  //   overall B
  //   gives B4
  //   B1-B4
  //   B1 is most significant
endmodule
