// Logisim project esfKeyT.circ as structural Verilog: 1 circuit, main circuit main
module main (
  input  [15:0] in_1,
  input  in_2,
  input  [31:0] in_3,
  input  [4:0] counter,
  input  [31:0] in_5,
  output [15:0] out_6,
  output [31:0] out_7,
  output [31:0] out_8
);

  wire [3:0] not_1_out;
  wire [31:0] shifter_1_out, shifter_2_out;

  not not_1 (not_1_out[0], in_2);
  not not_2 (not_1_out[2], in_2);
  not not_3 (not_1_out[3], in_2);
  Shifter #(.width(32)) shifter_1 (
    .in(in_5), .\dist ({in_2, not_1_out[3:2], in_2, not_1_out[0]}),
    .out({shifter_1_out[31:24], out_8[23:13], shifter_1_out[12:0]}));
  S0_main main_1 (
    .in_1(shifter_1_out[31]), .in_2(shifter_1_out[30]), .in_3(shifter_1_out[29]), .in_4(shifter_1_out[28]),
    .out_5(out_8[31]), .out_6(out_8[30]), .out_7(out_8[29]), .out_8(out_8[28]));
  S0_main main_2 (
    .in_1(shifter_1_out[27]), .in_2(shifter_1_out[26]), .in_3(shifter_1_out[25]), .in_4(shifter_1_out[24]),
    .out_5(out_8[27]), .out_6(out_8[26]), .out_7(out_8[25]), .out_8(out_8[24]));
  Shifter #(.width(32)) shifter_2 (
    .in(in_3), .\dist ({in_2, not_1_out[3:2], in_2, not_1_out[0]}),
    .out({shifter_2_out[31:27], out_7[26:13], shifter_2_out[12:0]}));
  assign out_7[31:27] = shifter_2_out[31:27] ^ counter;  // XOR_Gate xor_1, 5 bits wide

  assign out_6 = {in_1[2:0], in_5[31:19]};
  assign out_7[12:0] = in_1[15:3];
  assign out_8[12:0] = in_3[31:19];
endmodule
