// Logisim project Processor.circ as structural Verilog: 22 circuits, main circuit Control Unit
module Control_Unit (
  input  I_bit,
  input  [4:0] opcode,
  output isSt,
  output isLd,
  output isBeq,
  output isBgt,
  output isRet,
  output isImmediate,
  output isWb,
  output isUbranch,
  output isCall,
  output [12:0] ALUsignals
);

  wire and_6_out, and_7_out, and_8_out, and_9_out, and_10_out, and_12_out, and_13_out, nand_1_out;

  nand nand_1 (nand_1_out, opcode[0], opcode[1]);
  and and_1 (isSt, opcode[0], opcode[1], opcode[2], opcode[3], ~opcode[4]);  // AND_Gate
  and and_2 (isLd, ~opcode[0], opcode[1], opcode[2], opcode[3], ~opcode[4]);  // AND_Gate
  and and_3 (isBeq, ~opcode[0], ~opcode[1], ~opcode[2], ~opcode[3], opcode[4]);  // AND_Gate
  and and_4 (isBgt, opcode[0], ~opcode[1], ~opcode[2], ~opcode[3], opcode[4]);  // AND_Gate
  and and_5 (isRet, ~opcode[0], ~opcode[1], opcode[2], ~opcode[3], opcode[4]);  // AND_Gate
  and and_6 (and_6_out, opcode[0], ~opcode[1], opcode[2], ~opcode[4]);  // AND_Gate
  and and_7 (and_7_out, opcode[0], opcode[2], opcode[3], ~opcode[4]);  // AND_Gate
  and and_8 (and_8_out, opcode[4], nand_1_out);
  and and_9 (and_9_out, opcode[1], ~opcode[2], ~opcode[3], opcode[4]);  // AND_Gate
  and and_10 (and_10_out, ~opcode[0], ~opcode[1], opcode[2], ~opcode[3], opcode[4]);  // AND_Gate
  and and_11 (isCall, opcode[0], opcode[1], ~opcode[2], ~opcode[3], opcode[4]);  // AND_Gate
  and and_12 (and_12_out, ~opcode[0], ~opcode[1], ~opcode[2], ~opcode[3], ~opcode[4]);  // AND_Gate
  and and_13 (and_13_out, opcode[1], opcode[2], opcode[3], ~opcode[4]);  // AND_Gate
  and isSub (ALUsignals[2], opcode[0], ~opcode[1], ~opcode[2], ~opcode[3], ~opcode[4]);  // AND_Gate
  and isCmp (ALUsignals[0], opcode[0], ~opcode[1], opcode[2], ~opcode[3], ~opcode[4]);  // AND_Gate
  and isMul (ALUsignals[3], ~opcode[0], opcode[1], ~opcode[2], ~opcode[3], ~opcode[4]);  // AND_Gate
  and isDiv (ALUsignals[4], opcode[0], opcode[1], ~opcode[2], ~opcode[3], ~opcode[4]);  // AND_Gate
  and isMod (ALUsignals[5], ~opcode[0], ~opcode[1], opcode[2], ~opcode[3], ~opcode[4]);  // AND_Gate
  and isLsl (ALUsignals[7], ~opcode[0], opcode[1], ~opcode[2], opcode[3], ~opcode[4]);  // AND_Gate
  and isLsr (ALUsignals[8], opcode[0], opcode[1], ~opcode[2], opcode[3], ~opcode[4]);  // AND_Gate
  and isAsr (ALUsignals[9], ~opcode[0], ~opcode[1], opcode[2], opcode[3], ~opcode[4]);  // AND_Gate
  and isOr (ALUsignals[12], opcode[0], opcode[1], opcode[2], ~opcode[3], ~opcode[4]);  // AND_Gate
  and isAnd (ALUsignals[11], ~opcode[0], opcode[1], opcode[2], ~opcode[3], ~opcode[4]);  // AND_Gate
  and isNot (ALUsignals[10], ~opcode[0], ~opcode[1], ~opcode[2], opcode[3], ~opcode[4]);  // AND_Gate
  and isMov (ALUsignals[6], opcode[0], ~opcode[1], ~opcode[2], opcode[3], ~opcode[4]);  // AND_Gate
  or or_1 (isUbranch, and_9_out, and_10_out);
  or isAdd (ALUsignals[1], and_12_out, and_13_out);
  nor nor_1 (isWb, and_6_out, and_7_out, and_8_out);

  assign isImmediate = I_bit;

  // Notes on the sheet:
  //   op1
  //   op2
  //   op3
  //   op4
  //   op5
endmodule

module Register_File (
  input  Clock,
  input  Reset,
  input  [31:0] WriteD,
  input  [3:0] ReadA1,
  input  WriteE,
  input  [3:0] WriteA,
  input  [3:0] ReadA2,
  input  [3:0] DisplayA,
  output [31:0] ReadD1,
  output [31:0] ReadD2,
  output [31:0] DisplayD
);

  wire demultiplexer_1_out0, demultiplexer_1_out1, demultiplexer_1_out2, demultiplexer_1_out3,
       demultiplexer_1_out4, demultiplexer_1_out5, demultiplexer_1_out6, demultiplexer_1_out7,
       demultiplexer_1_out8, demultiplexer_1_out9, demultiplexer_1_out10, demultiplexer_1_out11,
       demultiplexer_1_out12, demultiplexer_1_out13, demultiplexer_1_out14, demultiplexer_1_out15,
       multiplexer_2_out, or_1_out, or_2_out;
  wire [31:0] multiplexer_1_out, r0_q, r1_q, r2_q, r3_q, r4_q, r5_q, r6_q, r7_q, r8_q, r9_q, r10_q, r11_q,
       r12_q, r13_q, r14_q, r15_q;

  Demultiplexer #(.select(4), .disabled(0), .enable("false")) demultiplexer_1 (
    .out0(demultiplexer_1_out0), .out1(demultiplexer_1_out1), .out2(demultiplexer_1_out2),
    .out3(demultiplexer_1_out3), .out4(demultiplexer_1_out4), .out5(demultiplexer_1_out5),
    .out6(demultiplexer_1_out6), .out7(demultiplexer_1_out7), .out8(demultiplexer_1_out8),
    .out9(demultiplexer_1_out9), .out10(demultiplexer_1_out10), .out11(demultiplexer_1_out11),
    .out12(demultiplexer_1_out12), .out13(demultiplexer_1_out13), .out14(demultiplexer_1_out14),
    .out15(demultiplexer_1_out15), .in(WriteE), .sel(WriteA));
  Multiplexer #(.width(32), .enable("false")) multiplexer_1 (
    .in0(WriteD), .in1(32'h3fffffc), .out(multiplexer_1_out), .sel(Reset));
  or or_1 (or_1_out, demultiplexer_1_out14, Reset);
  or or_2 (or_2_out, Clock, Reset);
  Multiplexer #(.enable("false")) multiplexer_2 (.in0(or_2_out), .out(multiplexer_2_out), .sel(1'b0));  // open: in1
  Register #(.width(32)) r0 (.D(WriteD), .en(demultiplexer_1_out0), .Q(r0_q), .clk(Clock), .clr(Reset));
  Register #(.width(32)) r1 (.D(WriteD), .en(demultiplexer_1_out1), .Q(r1_q), .clk(Clock), .clr(Reset));
  Register #(.width(32)) r2 (.D(WriteD), .en(demultiplexer_1_out2), .Q(r2_q), .clk(Clock), .clr(Reset));
  Register #(.width(32)) r3 (.D(WriteD), .en(demultiplexer_1_out3), .Q(r3_q), .clk(Clock), .clr(Reset));
  Register #(.width(32)) r4 (.D(WriteD), .en(demultiplexer_1_out4), .Q(r4_q), .clk(Clock), .clr(Reset));
  Register #(.width(32)) r5 (.D(WriteD), .en(demultiplexer_1_out5), .Q(r5_q), .clk(Clock), .clr(Reset));
  Register #(.width(32)) r6 (.D(WriteD), .en(demultiplexer_1_out6), .Q(r6_q), .clk(Clock), .clr(Reset));
  Register #(.width(32)) r7 (.D(WriteD), .en(demultiplexer_1_out7), .Q(r7_q), .clk(Clock), .clr(Reset));
  Register #(.width(32)) r8 (.D(WriteD), .en(demultiplexer_1_out8), .Q(r8_q), .clk(Clock), .clr(Reset));
  Register #(.width(32)) r9 (.D(WriteD), .en(demultiplexer_1_out9), .Q(r9_q), .clk(Clock), .clr(Reset));
  Register #(.width(32)) r10 (.D(WriteD), .en(demultiplexer_1_out10), .Q(r10_q), .clk(Clock), .clr(Reset));
  Register #(.width(32)) r11 (.D(WriteD), .en(demultiplexer_1_out11), .Q(r11_q), .clk(Clock), .clr(Reset));
  Register #(.width(32)) r12 (.D(WriteD), .en(demultiplexer_1_out12), .Q(r12_q), .clk(Clock), .clr(Reset));
  Register #(.width(32)) r13 (.D(WriteD), .en(demultiplexer_1_out13), .Q(r13_q), .clk(Clock), .clr(Reset));
  Register #(.width(32)) r14 (.D(multiplexer_1_out), .en(or_1_out), .Q(r14_q), .clk(multiplexer_2_out));  // open: clr
  Register #(.width(32)) r15 (.D(WriteD), .en(demultiplexer_1_out15), .Q(r15_q), .clk(Clock), .clr(Reset));
  Multiplexer #(.select(4), .width(32), .disabled(0), .enable("false")) multiplexer_3 (
    .in0(r0_q), .in1(r1_q), .in2(r2_q), .in3(r3_q), .in4(r4_q), .in5(r5_q), .in6(r6_q), .in7(r7_q),
    .in8(r8_q), .in9(r9_q), .in10(r10_q), .in11(r11_q), .in12(r12_q), .in13(r13_q), .in14(r14_q),
    .in15(r15_q), .out(ReadD1), .sel(ReadA1));
  Multiplexer #(.select(4), .width(32), .disabled(0), .enable("false")) multiplexer_4 (
    .in0(r0_q), .in1(r1_q), .in2(r2_q), .in3(r3_q), .in4(r4_q), .in5(r5_q), .in6(r6_q), .in7(r7_q),
    .in8(r8_q), .in9(r9_q), .in10(r10_q), .in11(r11_q), .in12(r12_q), .in13(r13_q), .in14(r14_q),
    .in15(r15_q), .out(ReadD2), .sel(ReadA2));
  Multiplexer #(.select(4), .width(32), .disabled(0), .enable("false")) multiplexer_5 (
    .in0(r0_q), .in1(r1_q), .in2(r2_q), .in3(r3_q), .in4(r4_q), .in5(r5_q), .in6(r6_q), .in7(r7_q),
    .in8(r8_q), .in9(r9_q), .in10(r10_q), .in11(r11_q), .in12(r12_q), .in13(r13_q), .in14(r14_q),
    .in15(r15_q), .out(DisplayD), .sel(DisplayA));
endmodule

module ALU (
  input  [31:0] A,
  input  [31:0] B,
  input  [12:0] ALUsignals,
  output [31:0] aluResult,
  output is,
  output is_2
);

  wire [31:0] adder_1_out, and_1_out, divider_1_out, divider_1_rem, multiplier_1_out, not_1_out, or_1_out,
       shifter_1_out, shifter_2_out, shifter_3_out, subtractor_1_out;

  Adder #(.width(32)) adder_1 (.a(A), .b(B), .out(adder_1_out));  // open: cin, cout
  Subtractor #(.width(32)) subtractor_1 (.a(A), .b(B), .out(subtractor_1_out));  // open: bin, bout
  Multiplier #(.width(32)) multiplier_1 (.a(A), .b(B), .out(multiplier_1_out));  // open: cin, cout
  Divider #(.width(32)) divider_1 (.a(A), .b(B), .out(divider_1_out), .rem(divider_1_rem));  // open: upper
  Comparator #(.width(32)) comparator_1 (.a(A), .b(B), .gt(is), .eq(is_2));  // open: lt
  Shifter #(.width(32)) shifter_1 (.in(A), .\dist (B[4:0]), .out(shifter_1_out));
  Shifter #(.width(32), .shift("lr")) shifter_2 (.in(A), .\dist (B[4:0]), .out(shifter_2_out));
  Shifter #(.width(32), .shift("ar")) shifter_3 (.in(A), .\dist (B[4:0]), .out(shifter_3_out));
  assign not_1_out = ~B;  // NOT_Gate not_1, 32 bits wide
  assign and_1_out = A & B;  // AND_Gate and_1, 32 bits wide
  assign or_1_out = A | B;  // OR_Gate or_1, 32 bits wide
  assign aluResult = ALUsignals[1] ? adder_1_out : 32'bz;  // Controlled_Buffer controlled_buffer_1
  assign aluResult = ALUsignals[2] ? subtractor_1_out : 32'bz;  // Controlled_Buffer controlled_buffer_2
  assign aluResult = ALUsignals[3] ? multiplier_1_out : 32'bz;  // Controlled_Buffer controlled_buffer_3
  assign aluResult = ALUsignals[4] ? divider_1_out : 32'bz;  // Controlled_Buffer controlled_buffer_4
  assign aluResult = ALUsignals[5] ? divider_1_rem : 32'bz;  // Controlled_Buffer controlled_buffer_5
  assign aluResult = ALUsignals[6] ? B : 32'bz;  // Controlled_Buffer controlled_buffer_6
  assign aluResult = ALUsignals[7] ? shifter_1_out : 32'bz;  // Controlled_Buffer controlled_buffer_7
  assign aluResult = ALUsignals[8] ? shifter_2_out : 32'bz;  // Controlled_Buffer controlled_buffer_8
  assign aluResult = ALUsignals[9] ? shifter_3_out : 32'bz;  // Controlled_Buffer controlled_buffer_9
  assign aluResult = ALUsignals[10] ? not_1_out : 32'bz;  // Controlled_Buffer controlled_buffer_10
  assign aluResult = ALUsignals[11] ? and_1_out : 32'bz;  // Controlled_Buffer controlled_buffer_11
  assign aluResult = ALUsignals[12] ? or_1_out : 32'bz;  // Controlled_Buffer controlled_buffer_12

  // Notes on the sheet:
  //   add
  //   sub
  //   mul
  //   div
  //   cmp
  //   lsr
  //   mod
  //   lsl
  //   asr
endmodule

module Flags (
  input  isCmp,
  input  is,
  input  is_2,
  output flags_GT,
  output flags_E
);

  D_Flip_Flop #(.trigger("high")) d_ff_1 (.clk(isCmp), .D(is), .Q(flags_GT));  // open: Qn, preset, en, reset
  D_Flip_Flop #(.trigger("high")) d_ff_2 (.clk(isCmp), .D(is_2), .Q(flags_E));  // open: Qn, preset, en, reset
endmodule

module Branch_Unit (
  input  isUBranch,
  input  isBeq,
  input  flags_E,
  input  isBgt,
  input  flags_GT,
  output isBranchTaken
);

  wire and_1_out, and_2_out;

  and and_1 (and_1_out, isBeq, flags_E);
  and and_2 (and_2_out, isBgt, flags_GT);
  or or_1 (isBranchTaken, isUBranch, and_1_out, and_2_out);
endmodule

module Memory_Unit (
  input  [31:0] MAR,
  input  isLd,
  input  [31:0] MDR,
  input  isSt,
  input  Clock,
  input  Reset,
  output [31:0] ldResult
);

  RAM #(.addrWidth(24), .dataWidth(32), .bus("separate")) ram_1 (
    .addr(MAR[25:2]), .din(MDR), .data(ldResult), .str(isSt), .clk(Clock), .ld(isLd), .clr(Reset));  // open: sel
endmodule

module Calculate_Immediate (
  input  [17:0] imm,
  output [31:0] immx
);

  wire [31:0] bit_extender_1_out, bit_extender_2_out, shifter_1_out;

  assign bit_extender_1_out = {{16{1'b0}}, imm[15:0]};  // Bit_Extender bit_extender_1
  assign bit_extender_2_out = {{16{imm[15]}}, imm[15:0]};  // Bit_Extender bit_extender_2
  Shifter #(.width(32)) shifter_1 (.in(bit_extender_1_out), .\dist (5'b10000), .out(shifter_1_out));
  Multiplexer #(.select(2), .width(32), .enable("false")) multiplexer_1 (
    .in0(bit_extender_2_out), .in1(bit_extender_1_out), .in2(shifter_1_out), .out(immx), .sel(imm[17:16]));  // open: in3

  // Notes on the sheet:
  //   modifier bits
  //   high
  //   default
  //   unsigned
endmodule

module IF_OF (
  input  [31:0] instruction,
  input  [31:0] PC,
  input  enable,
  input  clock,
  input  clear,
  output [31:0] instruction_2,
  output [31:0] PC_2
);

  Register #(.width(32), .trigger("falling")) register_1 (
    .D(instruction), .en(enable), .Q(instruction_2), .clk(clock), .clr(clear));
  Register #(.width(32), .trigger("falling")) register_2 (.D(PC), .en(enable), .Q(PC_2), .clk(clock), .clr(clear));
endmodule

module OF_EX (
  input  [31:0] PC,
  input  [31:0] branchTarget,
  input  [31:0] B,
  input  [31:0] A,
  input  [31:0] op2,
  input  [31:0] instruction,
  input  isSt,
  input  isLd,
  input  isBeq,
  input  isBgt,
  input  isRet,
  input  isImmediate,
  input  isWb,
  input  isUbranch,
  input  isCall,
  input  [12:0] ALUsignals,
  input  enable,
  input  clock,
  input  clear,
  output [31:0] PC_2,
  output [31:0] branchTarget_2,
  output [31:0] B_2,
  output [31:0] A_2,
  output [31:0] op2_2,
  output [31:0] instruction_2,
  output isSt_2,
  output isLd_2,
  output isBeq_2,
  output isBgt_2,
  output isRet_2,
  output isImmediate_2,
  output isWb_2,
  output isUbranch_2,
  output isCall_2,
  output [12:0] ALUsignals_2
);

  Register #(.width(32), .trigger("falling")) register_1 (.D(PC), .en(enable), .Q(PC_2), .clk(clock), .clr(clear));
  Register #(.width(32), .trigger("falling")) register_2 (
    .D(branchTarget), .en(enable), .Q(branchTarget_2), .clk(clock), .clr(clear));
  Register #(.width(32), .trigger("falling")) register_3 (.D(B), .en(enable), .Q(B_2), .clk(clock), .clr(clear));
  Register #(.width(32), .trigger("falling")) register_4 (.D(A), .en(enable), .Q(A_2), .clk(clock), .clr(clear));
  Register #(.width(32), .trigger("falling")) register_5 (.D(op2), .en(enable), .Q(op2_2), .clk(clock), .clr(clear));
  Register #(.width(32), .trigger("falling")) register_6 (
    .D(instruction), .en(enable), .Q(instruction_2), .clk(clock), .clr(clear));
  Register #(.width(9), .trigger("falling")) register_7 (
    .D({isCall, isUbranch, isWb, isImmediate, isRet, isBgt, isBeq, isLd, isSt}), .en(enable),
    .Q({isCall_2, isUbranch_2, isWb_2, isImmediate_2, isRet_2, isBgt_2, isBeq_2, isLd_2, isSt_2}),
    .clk(clock), .clr(clear));
  Register #(.width(13), .trigger("falling")) register_8 (
    .D(ALUsignals), .en(enable), .Q(ALUsignals_2), .clk(clock), .clr(clear));
endmodule

module EX_MA (
  input  [31:0] PC,
  input  [31:0] aluResult,
  input  [31:0] op2,
  input  [31:0] instruction,
  input  isSt,
  input  isLd,
  input  isBeq,
  input  isBgt,
  input  isRet,
  input  isImmediate,
  input  isWb,
  input  isUbranch,
  input  isCall,
  input  [12:0] ALUsignals,
  input  enable,
  input  clock,
  input  clear,
  output [31:0] PC_2,
  output [31:0] aluResult_2,
  output [31:0] op2_2,
  output [31:0] instruction_2,
  output isSt_2,
  output isLd_2,
  output isBeq_2,
  output isBgt_2,
  output isRet_2,
  output isImmediate_2,
  output isWb_2,
  output isUbranch_2,
  output isCall_2,
  output [12:0] ALUsignals_2
);

  Register #(.width(32), .trigger("falling")) register_1 (.D(PC), .en(enable), .Q(PC_2), .clk(clock), .clr(clear));
  Register #(.width(32), .trigger("falling")) register_2 (
    .D(aluResult), .en(enable), .Q(aluResult_2), .clk(clock), .clr(clear));
  Register #(.width(32), .trigger("falling")) register_3 (.D(op2), .en(enable), .Q(op2_2), .clk(clock), .clr(clear));
  Register #(.width(32), .trigger("falling")) register_4 (
    .D(instruction), .en(enable), .Q(instruction_2), .clk(clock), .clr(clear));
  Register #(.width(9), .trigger("falling")) register_5 (
    .D({isCall, isUbranch, isWb, isImmediate, isRet, isBgt, isBeq, isLd, isSt}), .en(enable),
    .Q({isCall_2, isUbranch_2, isWb_2, isImmediate_2, isRet_2, isBgt_2, isBeq_2, isLd_2, isSt_2}),
    .clk(clock), .clr(clear));
  Register #(.width(13), .trigger("falling")) register_6 (
    .D(ALUsignals), .en(enable), .Q(ALUsignals_2), .clk(clock), .clr(clear));
endmodule

module MA_RW (
  input  [31:0] PC,
  input  [31:0] ldResult,
  input  [31:0] aluResult,
  input  [31:0] instruction,
  input  isSt,
  input  isLd,
  input  isBeq,
  input  isBgt,
  input  isRet,
  input  isImmediate,
  input  isWb,
  input  isUbranch,
  input  isCall,
  input  [12:0] ALUsignals,
  input  enable,
  input  clock,
  input  clear,
  output [31:0] PC_2,
  output [31:0] ldResult_2,
  output [31:0] aluResult_2,
  output [31:0] instruction_2,
  output isSt_2,
  output isLd_2,
  output isBeq_2,
  output isBgt_2,
  output isRet_2,
  output isImmediate_2,
  output isWb_2,
  output isUbranch_2,
  output isCall_2,
  output [12:0] ALUsignals_2
);

  Register #(.width(32), .trigger("falling")) register_1 (.D(PC), .en(enable), .Q(PC_2), .clk(clock), .clr(clear));
  Register #(.width(32), .trigger("falling")) register_2 (
    .D(ldResult), .en(enable), .Q(ldResult_2), .clk(clock), .clr(clear));
  Register #(.width(32), .trigger("falling")) register_3 (
    .D(aluResult), .en(enable), .Q(aluResult_2), .clk(clock), .clr(clear));
  Register #(.width(32), .trigger("falling")) register_4 (
    .D(instruction), .en(enable), .Q(instruction_2), .clk(clock), .clr(clear));
  Register #(.width(9), .trigger("falling")) register_5 (
    .D({isCall, isUbranch, isWb, isImmediate, isRet, isBgt, isBeq, isLd, isSt}), .en(enable),
    .Q({isCall_2, isUbranch_2, isWb_2, isImmediate_2, isRet_2, isBgt_2, isBeq_2, isLd_2, isSt_2}),
    .clk(clock), .clr(clear));
  Register #(.width(13), .trigger("falling")) register_6 (
    .D(ALUsignals), .en(enable), .Q(ALUsignals_2), .clk(clock), .clr(clear));
endmodule

module lock_unit (
  input  [31:0] A,
  input  [31:0] B,
  output out_3
);

  wire A_opcode_c, and_1_out, and_2_out, and_3_out, B_opcode_prime_c, comparator_1_eq, comparator_2_eq,
       comparator_3_eq, comparator_4_eq, comparator_5_eq, comparator_6_eq, comparator_7_eq, comparator_8_eq,
       multiplexer_4_out, multiplexer_5_out, not_1_out, not_2_out, not_3_out, or_1_out, or_2_out;
  wire [3:0] multiplexer_1_out, multiplexer_2_out, multiplexer_3_out;

  Comparator #(.width(5), .mode("unsigned")) comparator_1 (
    .a(A[31:27]), .b(5'b01111), .eq(comparator_1_eq));  // open: gt, lt
  Comparator #(.width(5), .mode("unsigned")) comparator_2 (
    .a(A[31:27]), .b(5'b10100), .eq(comparator_2_eq));  // open: gt, lt
  Comparator #(.width(5), .mode("unsigned")) comparator_3 (
    .a(A[31:27]), .b(5'b01000), .eq(comparator_3_eq));  // open: gt, lt
  Comparator #(.width(5), .mode("unsigned")) comparator_4 (
    .a(A[31:27]), .b(5'b01001), .eq(comparator_4_eq));  // open: gt, lt
  not not_1 (not_1_out, comparator_5_eq);
  Comparator #(.width(5), .mode("unsigned")) comparator_5 (
    .a(A[31:27]), .b(5'b01111), .eq(comparator_5_eq));  // open: gt, lt
  Comparator #(.width(5), .mode("unsigned")) comparator_6 (
    .a(B[31:27]), .b(5'b10011), .eq(comparator_6_eq));  // open: gt, lt
  not not_2 (not_2_out, A_opcode_c);
  A_opcode A_opcode (.a1(A[31]), .a2(A[30]), .a3(A[29]), .a4(A[28]), .a5(A[27]), .c(A_opcode_c));
  or or_1 (or_1_out, comparator_3_eq, comparator_4_eq);
  B_opcode_prime B_opcode_prime (.b1(B[31]), .b2(B[30]), .b3(B[29]), .b4(B[28]), .b5(B[27]), .c(B_opcode_prime_c));
  Multiplexer #(.width(4)) multiplexer_1 (
    .in0(A[21:18]), .in1(4'b1111), .out(multiplexer_1_out), .sel(comparator_2_eq));  // open: en
  Multiplexer #(.width(4)) multiplexer_2 (
    .in0(A[17:14]), .in1(A[25:22]), .out(multiplexer_2_out), .sel(comparator_1_eq));  // open: en
  and and_1 (and_1_out, not_1_out, A[26]);
  Multiplexer #(.width(4)) multiplexer_3 (
    .in0(B[25:22]), .in1(4'b1111), .out(multiplexer_3_out), .sel(comparator_6_eq));  // open: en
  Multiplexer multiplexer_4 (.in0(1'b1), .in1(1'b0), .out(multiplexer_4_out), .sel(or_1_out));  // open: en
  Multiplexer multiplexer_5 (.in0(1'b1), .in1(1'b0), .out(multiplexer_5_out), .sel(and_1_out));  // open: en
  Comparator #(.width(4), .mode("unsigned")) comparator_7 (
    .a(multiplexer_2_out), .b(multiplexer_3_out), .eq(comparator_7_eq));  // open: gt, lt
  Comparator #(.width(4), .mode("unsigned")) comparator_8 (
    .a(multiplexer_1_out), .b(multiplexer_3_out), .eq(comparator_8_eq));  // open: gt, lt
  and and_2 (and_2_out, multiplexer_4_out, comparator_8_eq);
  and and_3 (and_3_out, multiplexer_5_out, comparator_7_eq);
  not not_3 (not_3_out, comparator_1_eq);
  or or_2 (or_2_out, and_2_out, and_3_out);
  and and_4 (out_3, or_2_out, not_2_out, B_opcode_prime_c, not_3_out);
endmodule

module A_opcode (
  input  a1,
  input  a2,
  input  a3,
  input  a4,
  input  a5,
  output c
);

  wire and_1_out, and_2_out, not_1_out, not_2_out, not_3_out, not_4_out;

  not not_1 (not_1_out, a1);
  not not_2 (not_2_out, a4);
  not not_3 (not_3_out, a2);
  not not_4 (not_4_out, a3);
  and and_1 (and_1_out, not_1_out, a2, a3, not_2_out, a5);
  and and_2 (and_2_out, a1, not_3_out, not_4_out);
  or or_1 (c, and_1_out, and_2_out);
endmodule

module B_opcode (
  input  a1,
  input  a2,
  input  a3,
  input  a4,
  input  a5,
  output c
);

  wire and_1_out, and_2_out, and_3_out, and_4_out, and_5_out, not_1_out, not_2_out, not_3_out, not_4_out,
       not_5_out, not_6_out, not_7_out, not_8_out, not_9_out, not_10_out, not_11_out, not_12_out;

  not not_1 (not_1_out, a1);
  not not_2 (not_2_out, a4);
  not not_3 (not_3_out, a1);
  not not_4 (not_4_out, a2);
  not not_5 (not_5_out, a3);
  not not_6 (not_6_out, a4);
  not not_7 (not_7_out, a2);
  not not_8 (not_8_out, a3);
  not not_9 (not_9_out, a5);
  not not_10 (not_10_out, a2);
  not not_11 (not_11_out, a4);
  not not_12 (not_12_out, a5);
  and and_1 (and_1_out, not_1_out, a3, not_2_out, a5);
  and and_2 (and_2_out, not_3_out, a2, a3, a5);
  and and_3 (and_3_out, a1, not_4_out, not_5_out, not_6_out);
  and and_4 (and_4_out, a1, not_7_out, not_8_out, not_9_out);
  and and_5 (and_5_out, a1, not_10_out, not_11_out, not_12_out);
  or or_1 (c, and_1_out, and_2_out, and_3_out, and_4_out, and_5_out);
endmodule

module forward_1 (
  input  [31:0] A,
  input  [31:0] B,
  output out_3
);

  wire comparator_1_eq, comparator_2_eq, comparator_3_eq, forward_1_a_check_1_c, forward_1_b_check_1_c,
       not_1_out, not_2_out;
  wire [3:0] multiplexer_1_out, multiplexer_2_out;

  Comparator #(.width(5), .mode("unsigned")) comparator_1 (
    .a(A[31:27]), .b(5'b10100), .eq(comparator_1_eq));  // open: gt, lt
  Comparator #(.width(5), .mode("unsigned")) comparator_2 (
    .a(B[31:27]), .b(5'b10011), .eq(comparator_2_eq));  // open: gt, lt
  forward_1_A_check forward_1_a_check_1 (
    .a1(A[31]), .a2(A[30]), .a3(A[29]), .a4(A[28]), .a5(A[27]), .c(forward_1_a_check_1_c));
  not not_1 (not_1_out, forward_1_a_check_1_c);
  not not_2 (not_2_out, forward_1_b_check_1_c);
  forward_1_B_check forward_1_b_check_1 (
    .a1(B[31]), .a2(B[30]), .a3(B[29]), .a4(B[28]), .a5(B[27]), .c(forward_1_b_check_1_c));
  Multiplexer #(.width(4)) multiplexer_1 (
    .in0(A[21:18]), .in1(4'b1111), .out(multiplexer_1_out), .sel(comparator_1_eq));  // open: en
  Multiplexer #(.width(4)) multiplexer_2 (
    .in0(B[25:22]), .in1(4'b1111), .out(multiplexer_2_out), .sel(comparator_2_eq));  // open: en
  Comparator #(.width(4), .mode("unsigned")) comparator_3 (
    .a(multiplexer_1_out), .b(multiplexer_2_out), .eq(comparator_3_eq));  // open: gt, lt
  and and_1 (out_3, not_1_out, comparator_3_eq, not_2_out);
endmodule

module forward_1_A_check (
  input  a1,
  input  a2,
  input  a3,
  input  a4,
  input  a5,
  output c
);

  wire and_1_out, and_2_out, and_3_out, not_1_out, not_2_out, not_3_out, not_4_out, not_5_out, not_6_out,
       not_7_out;

  not not_1 (not_1_out, a1);
  not not_2 (not_2_out, a3);
  not not_3 (not_3_out, a4);
  not not_4 (not_4_out, a1);
  not not_5 (not_5_out, a4);
  not not_6 (not_6_out, a2);
  not not_7 (not_7_out, a3);
  and and_1 (and_1_out, not_1_out, a2, not_2_out, not_3_out);
  and and_2 (and_2_out, not_4_out, a2, not_5_out, a5);
  and and_3 (and_3_out, a1, not_6_out, not_7_out);
  or or_1 (c, and_1_out, and_2_out, and_3_out);
endmodule

module forward_1_B_check (
  input  a1,
  input  a2,
  input  a3,
  input  a4,
  input  a5,
  output c
);

  wire and_1_out, and_2_out, and_3_out, and_4_out, and_5_out, not_1_out, not_2_out, not_3_out, not_4_out,
       not_5_out, not_6_out, not_7_out, not_8_out, not_9_out, not_10_out, not_11_out, not_12_out;

  not not_1 (not_1_out, a1);
  not not_2 (not_2_out, a4);
  not not_3 (not_3_out, a1);
  not not_4 (not_4_out, a2);
  not not_5 (not_5_out, a3);
  not not_6 (not_6_out, a4);
  not not_7 (not_7_out, a2);
  not not_8 (not_8_out, a3);
  not not_9 (not_9_out, a5);
  not not_10 (not_10_out, a2);
  not not_11 (not_11_out, a4);
  not not_12 (not_12_out, a5);
  and and_1 (and_1_out, not_1_out, a3, not_2_out, a5);
  and and_2 (and_2_out, not_3_out, a2, a3, a5);
  and and_3 (and_3_out, a1, not_4_out, not_5_out, not_6_out);
  and and_4 (and_4_out, a1, not_7_out, not_8_out, not_9_out);
  and and_5 (and_5_out, a1, not_10_out, not_11_out, not_12_out);
  or or_1 (c, and_1_out, and_2_out, and_3_out, and_4_out, and_5_out);
endmodule

module forward_2 (
  input  [31:0] A,
  input  [31:0] B,
  output out_3
);

  wire A_opcode_c, and_1_out, B_opcode_c, comparator_1_eq, comparator_2_eq, comparator_3_eq, comparator_4_eq,
       multiplexer_3_out, not_1_out, not_2_out, not_3_out;
  wire [3:0] multiplexer_1_out, multiplexer_2_out;

  Comparator #(.width(5), .mode("unsigned")) comparator_1 (
    .a(A[31:27]), .b(5'b01111), .eq(comparator_1_eq));  // open: gt, lt
  Comparator #(.width(5), .mode("unsigned")) comparator_2 (
    .a(A[31:27]), .b(5'b01111), .eq(comparator_2_eq));  // open: gt, lt
  not not_1 (not_1_out, comparator_2_eq);
  Comparator #(.width(5), .mode("unsigned")) comparator_3 (
    .a(B[31:27]), .b(5'b10011), .eq(comparator_3_eq));  // open: gt, lt
  not not_2 (not_2_out, A_opcode_c);
  A_opcode A_opcode (.a1(A[31]), .a2(A[30]), .a3(A[29]), .a4(A[28]), .a5(A[27]), .c(A_opcode_c));
  not not_3 (not_3_out, B_opcode_c);
  B_opcode B_opcode (.a1(B[31]), .a2(B[30]), .a3(B[29]), .a4(B[28]), .a5(B[27]), .c(B_opcode_c));
  Multiplexer #(.width(4)) multiplexer_1 (
    .in0(A[17:14]), .in1(A[25:22]), .out(multiplexer_1_out), .sel(comparator_1_eq));  // open: en
  and and_1 (and_1_out, not_1_out, A[26]);
  Multiplexer #(.width(4)) multiplexer_2 (
    .in0(B[25:22]), .in1(4'b1111), .out(multiplexer_2_out), .sel(comparator_3_eq));  // open: en
  Multiplexer multiplexer_3 (.in0(1'b1), .in1(1'b0), .out(multiplexer_3_out), .sel(and_1_out));  // open: en
  Comparator #(.width(4), .mode("unsigned")) comparator_4 (
    .a(multiplexer_1_out), .b(multiplexer_2_out), .eq(comparator_4_eq));  // open: gt, lt
  and and_2 (out_3, not_2_out, multiplexer_3_out, comparator_4_eq, not_3_out);
endmodule

module Control_handle (
  input  isSt,
  input  isLd,
  input  isBeq,
  input  isBgt,
  input  isRet,
  input  isImmediate,
  input  isWb,
  input  isUbranch,
  input  isCall,
  input  [12:0] ALUsignals,
  input  yes_con,
  output isSt_2,
  output isLd_2,
  output isBeq_2,
  output isBgt_2,
  output isRet_2,
  output isImmediate_2,
  output isWb_2,
  output isUbranch_2,
  output isCall_2,
  output [12:0] ALUsignals_2
);

  Multiplexer #(.width(9)) multiplexer_1 (
    .in0({isCall, isUbranch, isWb, isImmediate, isRet, isBgt, isBeq, isLd, isSt}), .in1({9{1'b0}}),
    .out({isCall_2, isUbranch_2, isWb_2, isImmediate_2, isRet_2, isBgt_2, isBeq_2, isLd_2, isSt_2}),
    .sel(yes_con));  // open: en
  Multiplexer #(.width(13)) multiplexer_2 (
    .in0(ALUsignals), .in1({13{1'b0}}), .out(ALUsignals_2), .sel(yes_con));  // open: en
endmodule

module Forwarding_Unit (
  input  [31:0] RW,
  input  [31:0] OF,
  input  [31:0] EX,
  input  [31:0] MA,
  output RW_OF_op1,
  output RW_OF_op2,
  output RW_EX_op1,
  output RW_EX_op2,
  output RW_MA_op2,
  output MA_EX_op1,
  output MA_EX_op2
);

  wire comparator_1_eq, logic_7_4_out_3, not_1_out;

  forward_1 logic_6 (.A(OF), .B(RW), .out_3(RW_OF_op1));
  forward_2 logic_7 (.A(OF), .B(RW), .out_3(RW_OF_op2));
  forward_1 logic_6_2 (.A(EX), .B(RW), .out_3(RW_EX_op1));
  forward_2 logic_7_2 (.A(EX), .B(RW), .out_3(RW_EX_op2));
  forward_2 logic_7_3 (.A(MA), .B(RW), .out_3(RW_MA_op2));
  forward_1 logic_6_3 (.A(EX), .B(MA), .out_3(MA_EX_op1));
  forward_2 logic_7_4 (.A(EX), .B(MA), .out_3(logic_7_4_out_3));
  Comparator #(.width(5), .mode("unsigned")) comparator_1 (
    .a(EX[31:27]), .b(5'b01111), .eq(comparator_1_eq));  // open: gt, lt
  not not_1 (not_1_out, comparator_1_eq);
  and and_1 (MA_EX_op2, not_1_out, logic_7_4_out_3);

  // Notes on the sheet:
  //   Logic 6: Conflict on the first operand (rs1/ra)
  //   Logic 7: Conflict on the second operand (rs2/rd)
endmodule

module B_opcode_prime (
  input  b1,
  input  b2,
  input  b3,
  input  b4,
  input  b5,
  output c
);

  wire not_1_out, not_2_out;

  not not_1 (not_1_out, b1);
  not not_2 (not_2_out, b5);
  and and_1 (c, not_1_out, b2, b3, b4, not_2_out);
endmodule

module Processor (
  input  Reset,
  input  [3:0] Display_Address
);

  wire alu_1_is, alu_1_is_2, Clock, comparator_1_eq, control_handle_1_isbeq_2, control_handle_1_isbgt_2,
       control_handle_1_iscall_2, control_handle_1_isimmediate_2, control_handle_1_isld_2,
       control_handle_1_isret_2, control_handle_1_isst_2, control_handle_1_isubranch_2,
       control_handle_1_iswb_2, control_unit_1_isbeq, control_unit_1_isbgt, control_unit_1_iscall,
       control_unit_1_isimmediate, control_unit_1_isld, control_unit_1_isret, control_unit_1_isst,
       control_unit_1_isubranch, control_unit_1_iswb, EX_MA_iscall_2, EX_MA_isld_2, EX_MA_isst_2,
       EX_MA_iswb_2, flags_1_flags_e, flags_1_flags_gt, isBranchTaken, MA_EX_op1, MA_EX_op2, MA_RW_iswb_2,
       not_1_out, not_2_out, OF_EX_isbeq_2, OF_EX_isbgt_2, OF_EX_iscall_2, OF_EX_isld_2, OF_EX_isret_2,
       OF_EX_isst_2, OF_EX_isubranch_2, OF_EX_iswb_2, RW_EX_op1, RW_EX_op2, RW_MA_op2, RW_OF_op1, RW_OF_op2,
       yes_con_OF_EX, yes_conflict;
  wire [0:0] and_1_out;
  wire [1:0] MA_RW_isld_2;
  wire [3:0] multiplexer_5_out, multiplexer_8_out, multiplexer_11_out, register_file_1_displayd_2;
  wire [12:0] control_handle_1_alusignals_2, control_unit_1_alusignals, OF_EX_alusignals_2;
  wire [31:0] adder_1_out, adder_2_out, adder_3_out, alu_1_aluresult, aluResult, bit_extender_1_out,
       calculate_immediate_1_immx, Data, EX_inst, EX_MA_op2_2, EX_MA_pc_2, IF_OF_instruction_2, IF_OF_pc_2,
       MA_inst, MA_RW_aluresult_2, MA_RW_ldresult_2, MA_RW_pc_2, memory_unit_1_ldresult, multiplexer_1_out,
       multiplexer_2_out, multiplexer_4_out, multiplexer_6_out, multiplexer_7_out, multiplexer_9_out,
       multiplexer_10_out, multiplexer_13_out, multiplexer_14_out, multiplexer_15_out, OF_EX_a_2, OF_EX_b_2,
       OF_EX_branchtarget_2, OF_EX_op2_2, OF_EX_pc_2, OF_inst, PC_q, register_file_1_displayd,
       register_file_1_readd1, register_file_1_readd2, rom_1_data, RW_inst, shifter_1_out;

  not not_1 (not_1_out, yes_con_OF_EX);
  Register #(.width(32), .trigger("falling")) PC (
    .D(multiplexer_1_out), .en(not_1_out), .Q(PC_q), .clk(Clock), .clr(Reset));
  Multiplexer #(.width(32), .enable("false")) multiplexer_1 (
    .in0(adder_1_out), .in1(multiplexer_2_out), .out(multiplexer_1_out), .sel(isBranchTaken));
  assign bit_extender_1_out = {{5{IF_OF_instruction_2[26]}}, IF_OF_instruction_2[26:0]};  // Bit_Extender bit_extender_1
  Adder #(.width(32)) adder_1 (.a(32'h4), .b(PC_q), .out(adder_1_out));  // open: cin, cout
  Shifter #(.width(32)) shifter_1 (.in(bit_extender_1_out), .\dist (5'b00010), .out(shifter_1_out));
  ALU alu_1 (
    .A(multiplexer_13_out), .B(multiplexer_15_out), .ALUsignals(OF_EX_alusignals_2),
    .aluResult(alu_1_aluresult), .is(alu_1_is), .is_2(alu_1_is_2));
  Adder #(.width(32)) adder_2 (.a(MA_RW_pc_2), .b(32'h4), .out(adder_2_out));  // open: cin, cout
  Calculate_Immediate calculate_immediate_1 (.imm(IF_OF_instruction_2[17:0]), .immx(calculate_immediate_1_immx));
  Adder #(.width(32)) adder_3 (.a(shifter_1_out), .b(IF_OF_pc_2), .out(adder_3_out));  // open: cin, cout
  Multiplexer #(.width(32), .enable("false")) multiplexer_2 (
    .in0(OF_EX_branchtarget_2), .in1(multiplexer_13_out), .out(multiplexer_2_out), .sel(OF_EX_isret_2));
  Memory_Unit memory_unit_1 (
    .MAR(aluResult), .ldResult(memory_unit_1_ldresult), .MDR(multiplexer_9_out), .isSt(EX_MA_isst_2),
    .isLd(EX_MA_isld_2), .Clock(Clock), .Reset(Reset));
  Multiplexer #(.select(2), .width(32), .enable("false")) multiplexer_3 (
    .in0(MA_RW_aluresult_2), .in1(MA_RW_ldresult_2), .in2(adder_2_out), .out(Data), .sel(MA_RW_isld_2));  // open: in3
  Clock u_Clock (.out(Clock));
  ROM #(.addrWidth(24), .dataWidth(32)) rom_1 (.addr(PC_q[25:2]), .data(rom_1_data));  // open: sel
  Multiplexer #(.width(32), .enable("false")) multiplexer_4 (
    .in0(multiplexer_6_out), .in1(calculate_immediate_1_immx), .out(multiplexer_4_out),
    .sel(control_unit_1_isimmediate));
  Flags flags_1 (
    .isCmp(OF_EX_alusignals_2[0]), .is(alu_1_is), .is_2(alu_1_is_2), .flags_GT(flags_1_flags_gt),
    .flags_E(flags_1_flags_e));
  Hex_Digit_Display hex_digit_display_1 (.value(register_file_1_displayd[31:28]));  // open: dp
  IF_OF IF_OF (
    .instruction(multiplexer_7_out), .PC(PC_q), .enable(not_1_out), .clock(Clock),
    .instruction_2(IF_OF_instruction_2), .PC_2(IF_OF_pc_2));  // open: clear
  Multiplexer #(.width(4), .enable("false")) multiplexer_5 (
    .in0(IF_OF_instruction_2[17:14]), .in1(IF_OF_instruction_2[25:22]), .out(multiplexer_5_out),
    .sel(control_unit_1_isst));
  Multiplexer #(.width(32)) multiplexer_6 (
    .in0(register_file_1_readd2), .in1(Data), .out(multiplexer_6_out), .sel(RW_OF_op2));  // open: en
  Multiplexer #(.width(32)) multiplexer_7 (
    .in0(rom_1_data), .in1(32'h68000000), .out(multiplexer_7_out), .sel(isBranchTaken));  // open: en
  Hex_Digit_Display hex_digit_display_2 (.value(register_file_1_displayd[27:24]));  // open: dp
  Multiplexer #(.width(4), .enable("false")) multiplexer_8 (
    .in0(IF_OF_instruction_2[21:18]), .in1(4'b1111), .out(multiplexer_8_out), .sel(control_unit_1_isret));
  Register_File register_file_1 (
    .ReadA1(multiplexer_8_out), .ReadA2(multiplexer_5_out), .WriteE(MA_RW_iswb_2), .WriteD(Data),
    .ReadD1(register_file_1_readd1), .ReadD2(register_file_1_readd2), .Clock(Clock), .Reset(Reset),
    .DisplayD({register_file_1_displayd[31:8], register_file_1_displayd_2, register_file_1_displayd[3:0]}),
    .DisplayA(Display_Address), .WriteA(multiplexer_11_out));
  Branch_Unit branch_unit_1 (
    .isBeq(OF_EX_isbeq_2), .isUBranch(OF_EX_isubranch_2), .flags_E(flags_1_flags_e), .isBgt(OF_EX_isbgt_2),
    .flags_GT(flags_1_flags_gt), .isBranchTaken(isBranchTaken));
  Multiplexer #(.width(32)) multiplexer_9 (
    .in0(EX_MA_op2_2), .in1(Data), .out(multiplexer_9_out), .sel(RW_MA_op2));  // open: en
  Hex_Digit_Display hex_digit_display_3 (.value(register_file_1_displayd[19:16]));  // open: dp
  Hex_Digit_Display hex_digit_display_4 (.value(register_file_1_displayd[23:20]));  // open: dp
  Hex_Digit_Display hex_digit_display_5 (.value(register_file_1_displayd[15:12]));  // open: dp
  Control_Unit control_unit_1 (
    .isSt(control_unit_1_isst), .isLd(control_unit_1_isld), .isBeq(control_unit_1_isbeq),
    .isBgt(control_unit_1_isbgt), .isRet(control_unit_1_isret), .I_bit(IF_OF_instruction_2[26]),
    .isImmediate(control_unit_1_isimmediate), .opcode(IF_OF_instruction_2[31:27]),
    .isWb(control_unit_1_iswb), .isUbranch(control_unit_1_isubranch), .isCall(control_unit_1_iscall),
    .ALUsignals(control_unit_1_alusignals));
  Hex_Digit_Display hex_digit_display_6 (.value(register_file_1_displayd[11:8]));  // open: dp
  Hex_Digit_Display hex_digit_display_7 (.value(register_file_1_displayd_2));  // open: dp
  Hex_Digit_Display hex_digit_display_8 (.value(register_file_1_displayd[3:0]));  // open: dp
  Multiplexer #(.width(32)) multiplexer_10 (
    .in0(register_file_1_readd1), .in1(Data), .out(multiplexer_10_out), .sel(RW_OF_op1));  // open: en
  Multiplexer #(.width(4), .enable("false")) multiplexer_11 (
    .in0(RW_inst[25:22]), .in1(4'b1111), .out(multiplexer_11_out), .sel(MA_RW_isld_2[1]));
  or or_1 (yes_conflict, yes_con_OF_EX, isBranchTaken);
  OF_EX OF_EX (
    .PC(IF_OF_pc_2), .branchTarget(adder_3_out), .B(multiplexer_4_out), .A(multiplexer_10_out),
    .op2(multiplexer_6_out), .instruction(OF_inst), .isSt(control_handle_1_isst_2),
    .isLd(control_handle_1_isld_2), .isBeq(control_handle_1_isbeq_2), .isBgt(control_handle_1_isbgt_2),
    .isRet(control_handle_1_isret_2), .isImmediate(control_handle_1_isimmediate_2),
    .isWb(control_handle_1_iswb_2), .isUbranch(control_handle_1_isubranch_2),
    .isCall(control_handle_1_iscall_2), .ALUsignals(control_handle_1_alusignals_2), .enable(1'b1),
    .clock(Clock), .PC_2(OF_EX_pc_2), .branchTarget_2(OF_EX_branchtarget_2), .B_2(OF_EX_b_2),
    .A_2(OF_EX_a_2), .op2_2(OF_EX_op2_2), .instruction_2(EX_inst), .isSt_2(OF_EX_isst_2),
    .isLd_2(OF_EX_isld_2), .isBeq_2(OF_EX_isbeq_2), .isBgt_2(OF_EX_isbgt_2), .isRet_2(OF_EX_isret_2),
    .isWb_2(OF_EX_iswb_2), .isUbranch_2(OF_EX_isubranch_2), .isCall_2(OF_EX_iscall_2),
    .ALUsignals_2(OF_EX_alusignals_2));  // open: clear, isImmediate_2
  Control_handle control_handle_1 (
    .isSt(control_unit_1_isst), .isLd(control_unit_1_isld), .isBeq(control_unit_1_isbeq),
    .isBgt(control_unit_1_isbgt), .isRet(control_unit_1_isret), .isImmediate(control_unit_1_isimmediate),
    .isWb(control_unit_1_iswb), .isUbranch(control_unit_1_isubranch), .isCall(control_unit_1_iscall),
    .ALUsignals(control_unit_1_alusignals), .yes_con(yes_conflict), .isSt_2(control_handle_1_isst_2),
    .isLd_2(control_handle_1_isld_2), .isBeq_2(control_handle_1_isbeq_2), .isBgt_2(control_handle_1_isbgt_2),
    .isRet_2(control_handle_1_isret_2), .isImmediate_2(control_handle_1_isimmediate_2),
    .isWb_2(control_handle_1_iswb_2), .isUbranch_2(control_handle_1_isubranch_2),
    .isCall_2(control_handle_1_iscall_2), .ALUsignals_2(control_handle_1_alusignals_2));
  lock_unit OF_EX_Data_lock (.A(IF_OF_instruction_2), .B(EX_inst), .out_3(yes_con_OF_EX));
  Multiplexer #(.width(32)) multiplexer_12 (
    .in0(IF_OF_instruction_2), .in1(32'h68000000), .out(OF_inst), .sel(yes_conflict));  // open: en
  Multiplexer #(.select(2), .width(32)) multiplexer_13 (
    .in0(OF_EX_a_2), .in1(Data), .in2(aluResult), .in3(aluResult), .out(multiplexer_13_out),
    .sel({MA_EX_op1, RW_EX_op1}));  // open: en
  Multiplexer #(.width(32)) multiplexer_14 (
    .in0(OF_EX_op2_2), .in1(Data), .out(multiplexer_14_out), .sel(RW_EX_op2));  // open: en
  EX_MA EX_MA (
    .PC(OF_EX_pc_2), .aluResult(alu_1_aluresult), .op2(multiplexer_14_out), .instruction(EX_inst),
    .isSt(OF_EX_isst_2), .isLd(OF_EX_isld_2), .isBeq(1'b1), .isBgt(1'b1), .isRet(1'b1), .isImmediate(1'b1),
    .isWb(OF_EX_iswb_2), .isUbranch(1'b1), .isCall(OF_EX_iscall_2), .ALUsignals(OF_EX_alusignals_2),
    .enable(1'b1), .clock(Clock), .PC_2(EX_MA_pc_2), .aluResult_2(aluResult), .op2_2(EX_MA_op2_2),
    .instruction_2(MA_inst), .isSt_2(EX_MA_isst_2), .isLd_2(EX_MA_isld_2), .isWb_2(EX_MA_iswb_2),
    .isCall_2(EX_MA_iscall_2));  // open: clear, isBeq_2, isBgt_2, isRet_2, isImmediate_2, isUbranch_2, ALUsignals_2
  Multiplexer #(.select(2), .width(32)) multiplexer_15 (
    .in0(OF_EX_b_2), .in1(Data), .in2(aluResult), .in3(aluResult), .out(multiplexer_15_out),
    .sel({MA_EX_op2, and_1_out[0]}));  // open: en
  MA_RW MA_RW (
    .PC(EX_MA_pc_2), .ldResult(memory_unit_1_ldresult), .aluResult(aluResult), .instruction(MA_inst),
    .isSt(1'b1), .isLd(EX_MA_isld_2), .isBeq(1'b1), .isBgt(1'b1), .isRet(1'b1), .isImmediate(1'b1),
    .isWb(EX_MA_iswb_2), .isUbranch(1'b1), .isCall(EX_MA_iscall_2), .ALUsignals(OF_EX_alusignals_2),
    .enable(1'b1), .clock(Clock), .PC_2(MA_RW_pc_2), .ldResult_2(MA_RW_ldresult_2),
    .aluResult_2(MA_RW_aluresult_2), .instruction_2(RW_inst), .isLd_2(MA_RW_isld_2[0]),
    .isWb_2(MA_RW_iswb_2), .isCall_2(MA_RW_isld_2[1]));  // open: clear, isSt_2, isBeq_2, isBgt_2, isRet_2, isImmediate_2, isUbranch_2, ALUsignals_2
  and and_1 (and_1_out[0], not_2_out, RW_EX_op2);
  Forwarding_Unit forwarding_unit_1 (
    .RW(RW_inst), .OF(OF_inst), .EX(EX_inst), .MA(MA_inst), .RW_OF_op1(RW_OF_op1), .RW_OF_op2(RW_OF_op2),
    .RW_EX_op1(RW_EX_op1), .RW_EX_op2(RW_EX_op2), .RW_MA_op2(RW_MA_op2), .MA_EX_op1(MA_EX_op1),
    .MA_EX_op2(MA_EX_op2));
  Comparator #(.width(5), .mode("unsigned")) comparator_1 (
    .a(EX_inst[31:27]), .b(5'b01111), .eq(comparator_1_eq));  // open: gt, lt
  not not_2 (not_2_out, comparator_1_eq);

  // Notes on the sheet:
  //   PIPELINED PROCESSOR
  //   isBranchTaken
  //   pc+4
  //   ALUsignals
  //   B
  //   pc
  //   branchTarget
  //   offset
  //   pc
  //   branchTarget
  //   A
  //   ALU
  //   aluResult
  //   MAR
  //   Memory
  //   Unit
  //   ldResult
  //   Instruction Memory
  //   calc immx
  //   imm
  //   isRet
  //   isBranchTaken
  //   is>
  //   is=
  //   MDR
  //   data
  //   contents of rom_1 (hex, n*v repeats v):
  //   4c000000 4c40000c 7c400000 4c400007 7c400004 4c40000b 7c400008 4c400003 7c40000c 4c400003 7c400010
  //   4c40000f 7c400014 4c800000 4cc00005 14cc0004 108c000 49810000 98000002 90000000 28188000 80000013
  //   1498000 1d540008 15540004 fb80010 7cb80000 7d780004 7db80008 7ff8000c 49814000 9ffffff5 75780004
  //   4940004 75b80008 9ffffff1 98000005 75780004 77f8000c 7b80010 a0000000 74b80000 75780004 5d40004
  //   75b80008 6100004 b188000 1f300004 7300001 4b430000 4ac1c000 48c08000 48420000 2c300000 8000001b
  //   280dc000 8000000e 282d8000 88000010 764c0000 76ac0000 28268000 88000002 90000004 7ea00000 6ec0004
  //   9000000c 7e600000 4cc0004 90000009 76ac0000 7ea00000 6ec0004 90000005 764c0000 7e600000 4cc0004
  //   90000001 f300001 6200004 97ffffe5 2c340000 80000007 76840000 7e880000 4440004 4880004 f740001
  //   97fffff9 a0000000
  //   immx
  //   Flags
  //   isCmp
  //   isLd
  //   isSt
  //   isLd
  //   isCall
  //   instruction
  //   rs1
  //   rs2
  //   rd
  //   isSt
  //   Register
  //   File
  //   op2
  //   isImmediate
  //   flags(GT)
  //   flags(E)
  //   isRet
  //   isWb
  //   E
  //   address
  //   A
  //   data
  //   D
  //   op1
  //   Branch
  //   Unit
  //   opcode
  //   I bit
  //   isBeq
  //   isBgt
  //   isUBranch
  //   Display Register
  //   CONTROL
  //   UNIT
  //   isCall
  //   rd
endmodule
