// Logisim project RoundFunction.circ as structural Verilog: 1 circuit, main circuit main
module main (
  input  [31:0] in_1,
  input  [31:0] in_2,
  output [31:0] out_3
);

  wire [3:0] xor_1_out_2, xor_1_out_3;
  wire [31:0] xor_1_out;

  S7 s7_1 (
    .a1(xor_1_out[31]), .a2(xor_1_out[30]), .a3(xor_1_out[29]), .a4(xor_1_out[28]), .b1(out_3[31]),
    .b2(out_3[23]), .b3(out_3[15]), .b4(out_3[7]));
  S6 s6_1 (
    .a1(xor_1_out[27]), .a2(xor_1_out[26]), .a3(xor_1_out[25]), .a4(xor_1_out[24]), .b1(out_3[30]),
    .b2(out_3[22]), .b3(out_3[14]), .b4(out_3[6]));
  S6 s6_2 (
    .a1(xor_1_out_3[3]), .a2(xor_1_out_3[2]), .a3(xor_1_out_3[1]), .a4(xor_1_out_3[0]), .b1(out_3[29]),
    .b2(out_3[21]), .b3(out_3[13]), .b4(out_3[5]));
  S4 s4_1 (
    .a1(xor_1_out_2[3]), .a2(xor_1_out_2[2]), .a3(xor_1_out_2[1]), .a4(xor_1_out_2[0]), .b1(out_3[28]),
    .b2(out_3[20]), .b3(out_3[12]), .b4(out_3[4]));
  assign {xor_1_out[31:24], xor_1_out_3, xor_1_out_2, xor_1_out[15:0]} = in_1 ^ in_2;  // XOR_Gate xor_1, 32 bits wide
  S3 s3_1 (
    .a1(xor_1_out[15]), .a2(xor_1_out[14]), .a3(xor_1_out[13]), .a4(xor_1_out[12]), .b1(out_3[27]),
    .b2(out_3[19]), .b3(out_3[11]), .b4(out_3[3]));
  S2 s2_1 (
    .a1(xor_1_out[11]), .a2(xor_1_out[10]), .a3(xor_1_out[9]), .a4(xor_1_out[8]), .b1(out_3[26]),
    .b2(out_3[18]), .b3(out_3[10]), .b4(out_3[2]));
  S1_main main_1 (
    .in_1(xor_1_out[7]), .in_2(xor_1_out[6]), .in_3(xor_1_out[5]), .in_4(xor_1_out[4]), .out_5(out_3[25]),
    .out_6(out_3[17]), .out_7(out_3[9]), .out_8(out_3[1]));
  S0_main main_2 (
    .in_1(xor_1_out[3]), .in_2(xor_1_out[2]), .in_3(xor_1_out[1]), .in_4(xor_1_out[0]), .out_5(out_3[24]),
    .out_6(out_3[16]), .out_7(out_3[8]), .out_8(out_3[0]));

  // Notes on the sheet:
  //   serpent S boxes
  //   permutations
endmodule
