// Logisim project KeyT.circ as structural Verilog: 1 circuit, main circuit main
module main (
  input  [15:0] in_1,
  input  [31:0] in_2,
  input  [31:0] in_3,
  input  [4:0] counter,
  output [31:0] out_5,
  output [15:0] out_6,
  output [31:0] out_7
);

  Sbox_main main_1 (
    .msb_to_lsb(in_3[18]), .in_2(in_3[17]), .in_3(in_3[16]), .in_4(in_3[15]), .out_5(out_6[15]),
    .out_6(out_6[14]), .out_7(out_6[13]), .out_8(out_6[12]));
  assign out_7[19:15] = in_2[6:2] ^ counter;  // XOR_Gate xor_1, 5 bits wide

  assign out_5 = {in_3[2:0], in_1, in_2[31:19]};
  assign out_6[11:0] = in_3[14:3];
  assign {out_7[31:20], out_7[14:0]} = {in_2[18:7], in_2[1:0], in_3[31:19]};

  // Notes on the sheet:
  //   msb
  //   lsb
  //   19
  //   15
endmodule
