// Logisim project SelectKey.circ as structural Verilog: 1 circuit, main circuit main
module main (
  input  [31:0] in_1,
  input  [31:0] in_2,
  input  [15:0] in_3,
  output [31:0] out_4,
  output [31:0] out_5
);


  assign out_4 = {in_3, in_1[31:16]};
  assign out_5 = {in_1[15:0], in_2[31:16]};

  // Notes on the sheet:
  //   80 bit Key
  //   msb
  //   lsb 
endmodule
